// Logisim project 2101CS09_1.circ as structural Verilog: 13 circuits, main circuit and gate
module and_gate (
  input  A,
  input  B,
  output Y
);

  wire transistor_1_out, transistor_4_out;

  Transistor transistor_1 (.in(1'b1), .out(transistor_1_out), .gate(B));
  Transistor transistor_2 (.in(1'b1), .out(transistor_1_out), .gate(A));
  Transistor #(.\type ("n")) transistor_3 (.in(transistor_4_out), .out(transistor_1_out), .gate(A));
  Transistor #(.\type ("n")) transistor_4 (.in(1'b0), .out(transistor_4_out), .gate(B));
  Transistor transistor_5 (.in(1'b1), .out(Y), .gate(transistor_1_out));
  Transistor #(.\type ("n")) transistor_6 (.in(1'b0), .out(Y), .gate(transistor_1_out));

  // Notes on the sheet:
  //   High  
  //   Ground
  //   and gate
endmodule

module nand_gate (
  input  in_1,
  input  in_2,
  output Output
);

  wire transistor_3_out;

  Transistor transistor_1 (.in(1'b1), .out(Output), .gate(in_2));
  Transistor #(.\type ("n")) transistor_2 (.in(transistor_3_out), .out(Output), .gate(in_1));
  Transistor #(.\type ("n")) transistor_3 (.in(1'b0), .out(transistor_3_out), .gate(in_2));
  Transistor transistor_4 (.in(1'b1), .out(Output), .gate(in_1));

  // Notes on the sheet:
  //   Inputs
  //   High voltage
  //   Ground
  //   NAND GATE
endmodule

module nor_gate (
  input  Inputs,
  input  in_2,
  output Output
);

  wire transistor_2_out;

  Transistor #(.\type ("n")) transistor_1 (.in(1'b0), .out(Output), .gate(in_2));
  Transistor transistor_2 (.in(1'b1), .out(transistor_2_out), .gate(Inputs));
  Transistor transistor_3 (.in(transistor_2_out), .out(Output), .gate(in_2));
  Transistor #(.\type ("n")) transistor_4 (.in(1'b0), .out(Output), .gate(Inputs));

  // Notes on the sheet:
  //   NOR GATE
  //   High voltage
  //   Ground
endmodule

module xor_gate (
  input  in_1,
  input  in_2,
  output Output
);

  wire transistor_1_out;

  Transistor transistor_1 (.in(1'b1), .out(transistor_1_out), .gate(in_1));
  Transistor #(.\type ("n")) transistor_2 (.in(1'b0), .out(transistor_1_out), .gate(in_1));
  Transistor transistor_3 (.in(in_1), .out(Output), .gate(in_2));
  Transistor #(.\type ("n")) transistor_4 (.in(transistor_1_out), .out(Output), .gate(in_2));

  // Notes on the sheet:
  //                        Inputs
  //               Highvoltage
  //   Ground
  //   XOR GATE
endmodule

module or_gate (
  input  Inputs,
  input  in_2,
  output Y
);

  wire transistor_1_out, transistor_2_out;

  Transistor #(.\type ("n")) transistor_1 (.in(1'b0), .out(transistor_1_out), .gate(in_2));
  Transistor transistor_2 (.in(1'b1), .out(transistor_2_out), .gate(Inputs));
  Transistor transistor_3 (.in(transistor_2_out), .out(transistor_1_out), .gate(in_2));
  Transistor #(.\type ("n")) transistor_4 (.in(1'b0), .out(transistor_1_out), .gate(Inputs));
  Transistor transistor_5 (.in(1'b1), .out(Y), .gate(transistor_1_out));
  Transistor #(.\type ("n")) transistor_6 (.in(1'b0), .out(Y), .gate(transistor_1_out));

  // Notes on the sheet:
  //   High voltage
  //   Ground
endmodule

module half_adder (
  input  A,
  input  B,
  output S,
  output C
);

  xor_gate xor_gate_1 (.in_1(A), .in_2(B), .Output(S));
  and_gate and_gate_1 (.A(A), .B(B), .Y(C));

  // Notes on the sheet:
  //   half adder
endmodule

module full_adder (
  input  in_1,
  input  in_2,
  input  in_3,
  output sum,
  output carry
);

  wire half_adder_1_c, half_adder_2_c, half_adder_2_s;

  half_adder half_adder_1 (.A(half_adder_2_s), .B(in_1), .S(sum), .C(half_adder_1_c));
  half_adder half_adder_2 (.A(in_2), .B(in_3), .S(half_adder_2_s), .C(half_adder_2_c));
  or_gate or_gate_1 (.Inputs(half_adder_1_c), .in_2(half_adder_2_c), .Y(carry));
endmodule

module two_bit (
  input  carry,
  input  b0,
  input  a0,
  input  a1,
  input  b1,
  output s0,
  output cout,
  output s1
);

  wire full_adder_1_carry;

  full_adder full_adder_1 (.in_1(carry), .in_2(b0), .in_3(a0), .sum(s0), .carry(full_adder_1_carry));
  full_adder full_adder_2 (.in_1(a1), .in_2(b1), .in_3(full_adder_1_carry), .sum(cout), .carry(s1));
endmodule

module four_bit (
  input  carry,
  input  b0,
  input  a0,
  input  a1,
  input  b1,
  input  in_6,
  input  in_7,
  input  in_8,
  input  in_9,
  output s0,
  output s1,
  output s2,
  output cout,
  output s3
);

  wire two_bit_1_cout;

  two_bit two_bit_1 (.carry(carry), .b0(b0), .a0(a0), .a1(a1), .b1(b1), .s0(s0), .cout(two_bit_1_cout), .s1(s1));
  two_bit two_bit_2 (.carry(in_6), .b0(two_bit_1_cout), .a0(in_7), .a1(in_8), .b1(in_9), .s0(s2), .cout(cout), .s1(s3));
endmodule

module _3_AND (
  input  A,
  input  B,
  input  C,
  output Y
);

  wire transistor_4_out, transistor_5_out;

  Transistor transistor_1 (.in(1'b0), .out(Y), .gate(A));
  Transistor transistor_2 (.in(1'b0), .out(Y), .gate(B));
  Transistor #(.\type ("n")) transistor_3 (.in(transistor_4_out), .out(Y), .gate(A));
  Transistor #(.\type ("n")) transistor_4 (.in(transistor_5_out), .out(transistor_4_out), .gate(B));
  Transistor #(.\type ("n")) transistor_5 (.in(1'b1), .out(transistor_5_out), .gate(C));
  Transistor transistor_6 (.in(1'b0), .out(Y), .gate(C));

  // Notes on the sheet:
  //   Inputs
  //   Grounded
  //   Highvoltage
  //   Grounded
  //   Grounded
endmodule

module half_subtractor (
  input  A,
  input  B,
  output D,
  output BORROW
);

  wire not_1_y;

  xor_gate xor_gate_1 (.in_1(A), .in_2(B), .Output(D));
  \not  not_1 (.in_1(A), .Y(not_1_y));
  and_gate and_gate_1 (.A(B), .B(not_1_y), .Y(BORROW));
endmodule

module \not  (
  input  in_1,
  output Y
);

  Transistor transistor_1 (.in(1'b1), .out(Y), .gate(in_1));
  Transistor #(.\type ("n")) transistor_2 (.in(1'b0), .out(Y), .gate(in_1));
endmodule

module _1_BIT__ALU (
  input  in_1,
  input  in_2,
  input  in_3,
  input  in_4,
  output carry_add,
  output carry_sub,
  output out
);

  wire and_gate_1_y, half_adder_1_s, half_subtractor_1_d, n3_and_1_y, n3_and_2_y, n3_and_3_y, n3_and_4_y,
       not_1_y, not_2_y, or_gate_1_y, or_gate_2_y, or_gate_3_y;

  half_adder half_adder_1 (.A(in_1), .B(in_2), .S(half_adder_1_s), .C(carry_add));
  half_subtractor half_subtractor_1 (.A(in_1), .B(in_2), .D(half_subtractor_1_d), .BORROW(carry_sub));
  and_gate and_gate_1 (.A(in_1), .B(in_2), .Y(and_gate_1_y));
  or_gate or_gate_1 (.Inputs(in_1), .in_2(in_2), .Y(or_gate_1_y));
  \not  not_1 (.in_1(in_3), .Y(not_1_y));
  \not  not_2 (.in_1(in_4), .Y(not_2_y));
  _3_AND u_3_and_1 (.A(half_adder_1_s), .B(not_1_y), .C(not_2_y), .Y(n3_and_1_y));
  _3_AND u_3_and_2 (.A(half_subtractor_1_d), .B(not_1_y), .C(in_4), .Y(n3_and_2_y));
  _3_AND u_3_and_3 (.A(and_gate_1_y), .B(in_3), .C(not_2_y), .Y(n3_and_3_y));
  _3_AND u_3_and_4 (.A(in_3), .B(or_gate_1_y), .C(in_4), .Y(n3_and_4_y));
  or_gate or_gate_2 (.Inputs(n3_and_1_y), .in_2(n3_and_2_y), .Y(or_gate_2_y));
  or_gate or_gate_3 (.Inputs(n3_and_3_y), .in_2(n3_and_4_y), .Y(or_gate_3_y));
  or_gate or_gate_4 (.Inputs(or_gate_2_y), .in_2(or_gate_3_y), .Y(out));
endmodule
