// Logisim project 2101CS09_2.circ as structural Verilog
module tb_not (
  input  in_1,
  output out_2
);

  Transistor transistor_1 (.in(1'b1), .out(out_2), .gate(in_1));
  Transistor #(.\type ("n")) transistor_2 (.in(1'b0), .out(out_2), .gate(in_1));
endmodule

module tb_nand (
  input  in_1,
  input  in_2,
  output out_3
);

  wire transistor_3_out;

  Transistor transistor_1 (.in(1'b1), .out(out_3), .gate(in_2));
  Transistor #(.\type ("n")) transistor_2 (.in(transistor_3_out), .out(out_3), .gate(in_1));
  Transistor #(.\type ("n")) transistor_3 (.in(1'b0), .out(transistor_3_out), .gate(in_2));
  Transistor transistor_4 (.in(1'b1), .out(out_3), .gate(in_1));
endmodule

module tb_and (
  input  in_1,
  input  in_2,
  output out_3
);

  wire transistor_1_out, transistor_3_out;

  Transistor transistor_1 (.in(1'b1), .out(transistor_1_out), .gate(in_2));
  Transistor #(.\type ("n")) transistor_2 (.in(transistor_3_out), .out(transistor_1_out), .gate(in_1));
  Transistor #(.\type ("n")) transistor_3 (.in(1'b0), .out(transistor_3_out), .gate(in_2));
  Transistor transistor_4 (.in(1'b1), .out(transistor_1_out), .gate(in_1));
  Transistor transistor_5 (.in(1'b1), .out(out_3), .gate(transistor_1_out));
  Transistor #(.\type ("n")) transistor_6 (.in(1'b0), .out(out_3), .gate(transistor_1_out));
endmodule

module tb_or (
  input  in_1,
  input  in_2,
  output out_3
);

  wire tb_nor_1_out_3;

  tb_nor tb_nor_1 (.in_1(in_1), .in_2(in_2), .out_3(tb_nor_1_out_3));
  tb_not tb_not_1 (.in_1(tb_nor_1_out_3), .out_2(out_3));
endmodule

module tb_xor (
  input  in_1,
  input  in_2,
  output out_3
);

  wire transistor_1_out;

  Transistor transistor_1 (.in(1'b1), .out(transistor_1_out), .gate(in_1));
  Transistor #(.\type ("n")) transistor_2 (.in(1'b0), .out(transistor_1_out), .gate(in_1));
  Transistor transistor_3 (.in(in_1), .out(out_3), .gate(in_2));
  Transistor #(.\type ("n")) transistor_4 (.in(transistor_1_out), .out(out_3), .gate(in_2));
endmodule

module tb_halfadder (
  input  A,
  input  B,
  output S,
  output C
);

  tb_xor tb_xor_1 (.in_1(A), .in_2(B), .out_3(S));
  tb_and tb_and_1 (.in_1(A), .in_2(B), .out_3(C));
endmodule

module Fulll_adder (
  input  A,
  input  B,
  input  C,
  output S,
  output C_2
);

  wire tb_and_1_out_3, tb_and_2_out_3, tb_and_3_out_3, tb_or_1_out_3, tb_xor_1_out_3;

  tb_and tb_and_1 (.in_1(A), .in_2(B), .out_3(tb_and_1_out_3));
  tb_and tb_and_2 (.in_1(B), .in_2(C), .out_3(tb_and_2_out_3));
  tb_and tb_and_3 (.in_1(A), .in_2(C), .out_3(tb_and_3_out_3));
  tb_xor tb_xor_1 (.in_1(A), .in_2(B), .out_3(tb_xor_1_out_3));
  tb_xor tb_xor_2 (.in_1(tb_xor_1_out_3), .in_2(C), .out_3(S));
  tb_or tb_or_1 (.in_1(tb_and_1_out_3), .in_2(tb_and_2_out_3), .out_3(tb_or_1_out_3));
  tb_or tb_or_2 (.in_1(tb_or_1_out_3), .in_2(tb_and_3_out_3), .out_3(C_2));
endmodule

module _2_Bit_Adder (
  input  A0,
  input  in_2,
  input  A1,
  input  in_4,
  output out_5,
  output out_6,
  output out_7,
  output out_8
);

  Fulll_adder fulll_adder_1 (.A(1'b0), .B(A0), .C(in_2), .S(out_5), .C_2(out_6));
  Fulll_adder fulll_adder_2 (.A(out_6), .B(A1), .C(in_4), .S(out_7), .C_2(out_8));
endmodule

module _4bit_adder (
  input  in_1,
  input  in_2,
  input  in_3,
  input  in_4,
  input  in_5,
  input  in_6,
  input  in_7,
  input  in_8,
  output out_9,
  output out_10,
  output out_11,
  output out_12,
  output out_13
);

  wire fulll_adder_1_c_2, fulll_adder_2_c_2;

  Fulll_adder fulll_adder_1 (.A(in_6), .B(in_5), .C(1'b0), .S(out_12), .C_2(fulll_adder_1_c_2));
  Fulll_adder fulll_adder_2 (.A(in_8), .B(in_7), .C(fulll_adder_1_c_2), .S(out_13), .C_2(fulll_adder_2_c_2));
  Fulll_adder fulll_adder_3 (.A(in_2), .B(in_1), .C(fulll_adder_2_c_2), .S(out_9), .C_2(in_3));
  Fulll_adder fulll_adder_4 (.A(in_4), .B(in_3), .C(in_3), .S(out_10), .C_2(out_11));
endmodule

module _1bit_ALU (
  input  in_1,
  input  in_2,
  input  in_3,
  input  [1:0] in_4,
  input  in_5,
  input  in_6,
  output out_7,
  output out_8
);

  wire multiplexer_1_p5, tb_nand_1_out_3, tb_not_1_out_2, tb_not_2_out_2, tb_or_1_out_3;
  wire [7:0] adder_1_out, multiplexer_1_p4, multiplexer_2_out;

  tb_not tb_not_1 (.out_2(tb_not_1_out_2));  // open: in_1
  tb_not tb_not_2 (.in_1(in_1), .out_2(tb_not_2_out_2));
  // Multiplexer multiplexer_1: pin names not known; wires that end beside it: tb_not_1_out_2, in_2, in_5, multiplexer_1_p4, multiplexer_1_p5, multiplexer_1_p5
  Multiplexer multiplexer_2 (.in0(tb_not_2_out_2), .in1(in_1), .out(multiplexer_2_out[0]), .sel(in_6));  // open: en
  tb_nand tb_nand_1 (.in_1(multiplexer_1_p4[0]), .in_2(multiplexer_2_out[0]), .out_3(tb_nand_1_out_3));
  tb_or tb_or_1 (.in_1(multiplexer_1_p4[0]), .in_2(multiplexer_2_out[0]), .out_3(tb_or_1_out_3));
  Adder adder_1 (.a(multiplexer_1_p4), .b(multiplexer_2_out), .out(adder_1_out), .cin(in_3), .cout(out_8));
  // Multiplexer multiplexer_3: pin names not known; wires that end beside it: tb_nand_1_out_3, tb_or_1_out_3, adder_1_out, in_4, out_7
  // Pins of 1 and 8 bits meet at multiplexer_1_p4
  // Pins of 1 and 8 bits meet at multiplexer_2_out
endmodule

module _2_bit_decoder (
  input  in_1,
  input  in_2,
  output D0,
  output D1,
  output D2,
  output D3
);

  wire tb_not_1_out_2, tb_not_2_out_2;

  tb_not tb_not_1 (.in_1(in_1), .out_2(tb_not_1_out_2));
  tb_not tb_not_2 (.in_1(in_2), .out_2(tb_not_2_out_2));
  tb_and tb_and_1 (.in_1(tb_not_1_out_2), .in_2(tb_not_2_out_2), .out_3(D0));
  tb_and tb_and_2 (.in_1(tb_not_2_out_2), .in_2(in_1), .out_3(D1));
  tb_and tb_and_3 (.in_1(tb_not_1_out_2), .in_2(in_2), .out_3(D2));
  tb_and tb_and_4 (.in_1(in_2), .in_2(in_1), .out_3(D3));
endmodule

module tb_nor (
  input  in_1,
  input  in_2,
  output out_3
);

  wire transistor_2_out;

  Transistor #(.\type ("n")) transistor_1 (.in(1'b0), .out(out_3), .gate(in_2));
  Transistor transistor_2 (.in(1'b1), .out(transistor_2_out), .gate(in_1));
  Transistor transistor_3 (.in(transistor_2_out), .out(out_3), .gate(in_2));
  Transistor #(.\type ("n")) transistor_4 (.in(1'b0), .out(out_3), .gate(in_1));

  // Notes on the sheet:
  //   Inputs
  //   NOR GATE
  //   Ground
  //   High voltage
  //   Output
endmodule

module _2_bit_multiplier (
  input  X0,
  input  Y0,
  input  X1,
  input  Y1,
  output P0,
  output P1,
  output P2,
  output P3
);

  wire tb_and_2_out_3, tb_and_3_out_3, tb_and_4_out_3, tb_halfadder_1_c;

  tb_and tb_and_1 (.in_1(X0), .in_2(Y0), .out_3(P0));
  tb_and tb_and_2 (.in_1(X0), .in_2(Y1), .out_3(tb_and_2_out_3));
  tb_and tb_and_3 (.in_1(X1), .in_2(Y0), .out_3(tb_and_3_out_3));
  tb_and tb_and_4 (.in_1(Y1), .in_2(X1), .out_3(tb_and_4_out_3));
  tb_halfadder tb_halfadder_1 (.A(tb_and_3_out_3), .B(tb_and_2_out_3), .S(P1), .C(tb_halfadder_1_c));
  tb_halfadder tb_halfadder_2 (.A(tb_and_4_out_3), .B(tb_halfadder_1_c), .S(P2), .C(P3));
endmodule

module _3_bit_multiplier (
  input  X0,
  input  Y0,
  input  X1,
  input  Y1,
  input  X2,
  input  Y2,
  output P0,
  output P1,
  output P3,
  output P2,
  output P4,
  output p5
);

  wire fulll_adder_1_c_2, fulll_adder_1_s, fulll_adder_2_c_2, tb_and_2_out_3, tb_and_3_out_3, tb_and_4_out_3,
       tb_and_5_out_3, tb_and_6_out_3, tb_and_7_out_3, tb_and_8_out_3, tb_and_9_out_3, tb_halfadder_1_c,
       tb_halfadder_2_c, tb_halfadder_2_s, tb_halfadder_3_c;

  tb_and tb_and_1 (.in_1(X0), .in_2(Y0), .out_3(P0));
  tb_and tb_and_2 (.in_1(Y0), .in_2(X1), .out_3(tb_and_2_out_3));
  tb_and tb_and_3 (.in_1(X1), .in_2(Y1), .out_3(tb_and_3_out_3));
  tb_and tb_and_4 (.in_1(X0), .in_2(Y1), .out_3(tb_and_4_out_3));
  tb_and tb_and_5 (.in_1(Y2), .in_2(X1), .out_3(tb_and_5_out_3));
  tb_and tb_and_6 (.in_1(X0), .in_2(Y2), .out_3(tb_and_6_out_3));
  tb_and tb_and_7 (.in_1(Y0), .in_2(X2), .out_3(tb_and_7_out_3));
  tb_and tb_and_8 (.in_1(Y1), .in_2(X2), .out_3(tb_and_8_out_3));
  tb_and tb_and_9 (.in_1(X2), .in_2(Y2), .out_3(tb_and_9_out_3));
  tb_halfadder tb_halfadder_1 (.A(tb_and_2_out_3), .B(tb_and_4_out_3), .S(P1), .C(tb_halfadder_1_c));
  tb_halfadder tb_halfadder_2 (.A(tb_and_8_out_3), .B(fulll_adder_1_c_2), .S(tb_halfadder_2_s), .C(tb_halfadder_2_c));
  tb_halfadder tb_halfadder_3 (.A(fulll_adder_1_s), .B(tb_and_6_out_3), .S(P2), .C(tb_halfadder_3_c));
  Fulll_adder fulll_adder_1 (
    .A(tb_halfadder_1_c), .B(tb_and_7_out_3), .C(tb_and_3_out_3), .S(fulll_adder_1_s), .C_2(fulll_adder_1_c_2));
  Fulll_adder fulll_adder_2 (
    .A(tb_halfadder_2_s), .B(tb_and_5_out_3), .C(tb_halfadder_3_c), .S(P3), .C_2(fulll_adder_2_c_2));
  Fulll_adder fulll_adder_3 (.A(fulll_adder_2_c_2), .B(tb_halfadder_2_c), .C(tb_and_9_out_3), .S(P4), .C_2(p5));
endmodule

module multiplexer (
  input  in_1,
  input  in_2,
  input  in_3,
  input  in_4,
  input  in_5,
  input  in_6,
  output out_7
);

  wire n3_input_and_1_y, n3_input_and_2_y, n3_input_and_3_y, n3_input_and_4_y, n3_input_or_1_out_4,
       tb_not_1_out_2, tb_not_2_out_2;

  tb_not tb_not_1 (.in_1(in_6), .out_2(tb_not_1_out_2));
  tb_not tb_not_2 (.in_1(in_5), .out_2(tb_not_2_out_2));
  _3_input_and u_3_input_and_1 (.A(in_1), .B(tb_not_1_out_2), .C(tb_not_2_out_2), .Y(n3_input_and_1_y));
  _3_input_and u_3_input_and_2 (.A(in_2), .B(tb_not_1_out_2), .C(in_5), .Y(n3_input_and_2_y));
  _3_input_and u_3_input_and_3 (.A(in_3), .B(in_6), .C(tb_not_2_out_2), .Y(n3_input_and_3_y));
  _3_input_and u_3_input_and_4 (.A(in_4), .B(in_6), .C(in_5), .Y(n3_input_and_4_y));
  _3_input_or u_3_input_or_1 (
    .in_1(n3_input_and_1_y), .in_2(n3_input_and_2_y), .in_3(n3_input_and_3_y), .out_4(n3_input_or_1_out_4));
  tb_or tb_or_1 (.in_1(n3_input_or_1_out_4), .in_2(n3_input_and_4_y), .out_3(out_7));
endmodule

module _3_input_and (
  input  A,
  input  B,
  input  C,
  output Y
);

  wire transistor_4_out, transistor_5_out;

  Transistor transistor_1 (.in(1'b0), .out(Y), .gate(A));
  Transistor transistor_2 (.in(1'b0), .out(Y), .gate(B));
  Transistor #(.\type ("n")) transistor_3 (.in(transistor_4_out), .out(Y), .gate(A));
  Transistor #(.\type ("n")) transistor_4 (.in(transistor_5_out), .out(transistor_4_out), .gate(B));
  Transistor #(.\type ("n")) transistor_5 (.in(1'b1), .out(transistor_5_out), .gate(C));
  Transistor transistor_6 (.in(1'b0), .out(Y), .gate(C));
endmodule

module _3_input_or (
  input  in_1,
  input  in_2,
  input  in_3,
  output out_4
);

  wire tb_or_1_out_3;

  tb_or tb_or_1 (.in_1(in_1), .in_2(in_2), .out_3(tb_or_1_out_3));
  tb_or tb_or_2 (.in_1(tb_or_1_out_3), .in_2(in_3), .out_3(out_4));
endmodule

module _4_bit_adder_subtractor (
  input  sel,
  input  A0,
  input  B0,
  input  A1,
  input  B1,
  input  A2,
  input  B2,
  input  A3,
  input  B3,
  output S0,
  output S1,
  output S2,
  output S3,
  output V,
  output C
);

  wire fulll_adder_1_c_2, fulll_adder_2_c_2, fulll_adder_3_c_2, tb_xor_1_out_3, tb_xor_2_out_3,
       tb_xor_3_out_3, tb_xor_4_out_3;

  tb_xor tb_xor_1 (.in_1(sel), .in_2(B0), .out_3(tb_xor_1_out_3));
  tb_xor tb_xor_2 (.in_1(sel), .in_2(B1), .out_3(tb_xor_2_out_3));
  tb_xor tb_xor_3 (.in_1(sel), .in_2(B2), .out_3(tb_xor_3_out_3));
  tb_xor tb_xor_4 (.in_1(sel), .in_2(B3), .out_3(tb_xor_4_out_3));
  Fulll_adder fulll_adder_1 (.A(sel), .B(A0), .C(tb_xor_1_out_3), .S(S0), .C_2(fulll_adder_1_c_2));
  Fulll_adder fulll_adder_2 (.A(fulll_adder_1_c_2), .B(A1), .C(tb_xor_2_out_3), .S(S1), .C_2(fulll_adder_2_c_2));
  Fulll_adder fulll_adder_3 (.A(fulll_adder_2_c_2), .B(A2), .C(tb_xor_3_out_3), .S(S2), .C_2(fulll_adder_3_c_2));
  Fulll_adder fulll_adder_4 (.A(A3), .B(fulll_adder_3_c_2), .C(tb_xor_4_out_3), .S(S3), .C_2(C));
  tb_xor tb_xor_5 (.in_1(C), .in_2(fulll_adder_3_c_2), .out_3(V));
endmodule

module _8_bit_multiplier (
  input  in_1,
  input  in_2,
  input  in_3,
  input  in_4,
  input  in_5,
  input  in_6,
  input  in_7,
  input  in_8,
  input  in_9,
  input  in_10,
  input  in_11,
  input  in_12,
  input  in_13,
  input  in_14,
  input  in_15,
  input  in_16,
  input  in_17,
  output out_18,
  output out_19,
  output out_20,
  output out_21,
  output out_22,
  output out_23,
  output out_24,
  output out_25
);

  _2_bit_multiplexer u_2_bit_multiplexer_1 (.in_1(in_9), .in_2(in_1), .in_3(in_17), .out_4(out_24));
  _2_bit_multiplexer u_2_bit_multiplexer_2 (.in_1(in_11), .in_2(in_3), .in_3(in_17), .out_4(out_22));
  _2_bit_multiplexer u_2_bit_multiplexer_3 (.in_1(in_10), .in_2(in_2), .in_3(in_17), .out_4(out_25));
  _2_bit_multiplexer u_2_bit_multiplexer_4 (.in_1(in_12), .in_2(in_4), .in_3(in_17), .out_4(out_23));
  _2_bit_multiplexer u_2_bit_multiplexer_5 (.in_1(in_5), .in_2(in_5), .in_3(in_17), .out_4(out_18));
  _2_bit_multiplexer u_2_bit_multiplexer_6 (.in_1(in_14), .in_2(in_6), .in_3(in_17), .out_4(out_19));
  _2_bit_multiplexer u_2_bit_multiplexer_7 (.in_1(in_15), .in_2(in_7), .in_3(in_17), .out_4(out_20));
  _2_bit_multiplexer u_2_bit_multiplexer_8 (.in_1(in_16), .in_2(in_8), .in_3(in_17), .out_4(out_21));

  assign in_13 = in_5;
endmodule

module _2_bit_multiplexer (
  input  in_1,
  input  in_2,
  input  in_3,
  output out_4
);

  wire tb_and_1_out_3, tb_and_2_out_3, tb_not_1_out_2;

  tb_not tb_not_1 (.in_1(in_2), .out_2(tb_not_1_out_2));
  tb_and tb_and_1 (.in_1(in_1), .in_2(in_2), .out_3(tb_and_1_out_3));
  tb_and tb_and_2 (.in_1(tb_not_1_out_2), .in_2(in_3), .out_3(tb_and_2_out_3));
  tb_or tb_or_1 (.in_1(tb_and_1_out_3), .in_2(tb_and_2_out_3), .out_3(out_4));
endmodule

module _8_bit_adder_subtractor (
  input  sel,
  input  A0,
  input  B0,
  input  A1,
  input  B1,
  input  A2,
  input  B2,
  input  A3,
  input  B3,
  input  A4,
  input  B4,
  input  A5,
  input  B5,
  input  A6,
  input  B6,
  input  A7,
  input  B7,
  output S0,
  output S1,
  output S2,
  output S3,
  output S4,
  output S5,
  output S6,
  output S7,
  output V,
  output C
);

  wire fulll_adder_1_c_2, fulll_adder_3_c_2, fulll_adder_4_c_2, fulll_adder_5_c_2, fulll_adder_6_c_2,
       fulll_adder_7_c_2, fulll_adder_8_c_2, tb_xor_1_out_3, tb_xor_2_out_3, tb_xor_3_out_3, tb_xor_4_out_3,
       tb_xor_5_out_3, tb_xor_6_out_3, tb_xor_7_out_3, tb_xor_8_out_3;

  tb_xor tb_xor_1 (.in_1(sel), .in_2(B0), .out_3(tb_xor_1_out_3));
  tb_xor tb_xor_2 (.in_1(sel), .in_2(B1), .out_3(tb_xor_2_out_3));
  tb_xor tb_xor_3 (.in_1(sel), .in_2(B2), .out_3(tb_xor_3_out_3));
  tb_xor tb_xor_4 (.in_1(sel), .in_2(B3), .out_3(tb_xor_4_out_3));
  tb_xor tb_xor_5 (.in_1(sel), .in_2(B4), .out_3(tb_xor_5_out_3));
  tb_xor tb_xor_6 (.in_1(sel), .in_2(B5), .out_3(tb_xor_6_out_3));
  tb_xor tb_xor_7 (.in_1(sel), .in_2(B6), .out_3(tb_xor_7_out_3));
  tb_xor tb_xor_8 (.in_1(sel), .in_2(B7), .out_3(tb_xor_8_out_3));
  Fulll_adder fulll_adder_1 (.A(fulll_adder_5_c_2), .B(A3), .C(tb_xor_4_out_3), .S(S3), .C_2(fulll_adder_1_c_2));
  Fulll_adder fulll_adder_2 (.A(A7), .B(fulll_adder_8_c_2), .C(tb_xor_8_out_3), .S(S7), .C_2(C));
  Fulll_adder fulll_adder_3 (.A(sel), .B(A0), .C(tb_xor_1_out_3), .S(S0), .C_2(fulll_adder_3_c_2));
  Fulll_adder fulll_adder_4 (.A(fulll_adder_3_c_2), .B(A1), .C(tb_xor_2_out_3), .S(S1), .C_2(fulll_adder_4_c_2));
  Fulll_adder fulll_adder_5 (.A(fulll_adder_4_c_2), .B(A2), .C(tb_xor_3_out_3), .S(S2), .C_2(fulll_adder_5_c_2));
  Fulll_adder fulll_adder_6 (.A(fulll_adder_1_c_2), .B(A4), .C(tb_xor_5_out_3), .S(S4), .C_2(fulll_adder_6_c_2));
  Fulll_adder fulll_adder_7 (.A(fulll_adder_6_c_2), .B(A5), .C(tb_xor_6_out_3), .S(S5), .C_2(fulll_adder_7_c_2));
  Fulll_adder fulll_adder_8 (.A(fulll_adder_7_c_2), .B(A6), .C(tb_xor_7_out_3), .S(S6), .C_2(fulll_adder_8_c_2));
  tb_xor tb_xor_9 (.in_1(C), .in_2(fulll_adder_8_c_2), .out_3(V));
endmodule

module _8_bit_comparator (
  input  [7:0] B,
  input  [7:0] A,
  output A_B,
  output A_B_2,
  output A_B_3
);

  wire n4_bit_comparator_1_a_b, n4_bit_comparator_1_a_b_2, n4_bit_comparator_1_a_b_3,
       n4_bit_comparator_2_a_b, n4_bit_comparator_2_a_b_2, n4_bit_comparator_2_a_b_3, tb_and_1_out_3,
       tb_and_2_out_3;

  tb_or tb_or_1 (.in_1(tb_and_1_out_3), .in_2(n4_bit_comparator_1_a_b), .out_3(A_B));
  tb_and tb_and_1 (.in_1(n4_bit_comparator_2_a_b), .in_2(n4_bit_comparator_1_a_b_3), .out_3(tb_and_1_out_3));
  _4_bit_comparator u_4_bit_comparator_1 (
    .B(B[7:4]), .A(A[7:4]), .A_B(n4_bit_comparator_1_a_b), .A_B_2(n4_bit_comparator_1_a_b_2),
    .A_B_3(n4_bit_comparator_1_a_b_3));
  tb_and tb_and_2 (.in_1(n4_bit_comparator_2_a_b_2), .in_2(n4_bit_comparator_1_a_b_3), .out_3(tb_and_2_out_3));
  tb_or tb_or_2 (.in_1(tb_and_2_out_3), .in_2(n4_bit_comparator_1_a_b_2), .out_3(A_B_2));
  _4_bit_comparator u_4_bit_comparator_2 (
    .B(B[3:0]), .A(A[3:0]), .A_B(n4_bit_comparator_2_a_b), .A_B_2(n4_bit_comparator_2_a_b_2),
    .A_B_3(n4_bit_comparator_2_a_b_3));
  tb_and tb_and_3 (.in_1(n4_bit_comparator_2_a_b_3), .in_2(n4_bit_comparator_1_a_b_3), .out_3(A_B_3));
endmodule

module _1bit_comparator (
  input  A,
  input  B,
  output A_B,
  output A_B_2,
  output A_B_3
);

  wire tb_and_1_out_3, tb_and_2_out_3, tb_not_1_out_2, tb_not_2_out_2;

  tb_not tb_not_1 (.in_1(A), .out_2(tb_not_1_out_2));
  tb_not tb_not_2 (.in_1(B), .out_2(tb_not_2_out_2));
  tb_and tb_and_1 (.in_1(A), .in_2(B), .out_3(tb_and_1_out_3));
  tb_and tb_and_2 (.in_1(tb_not_1_out_2), .in_2(tb_not_2_out_2), .out_3(tb_and_2_out_3));
  tb_and tb_and_3 (.in_1(A), .in_2(tb_not_2_out_2), .out_3(A_B_2));
  tb_and tb_and_4 (.in_1(tb_not_1_out_2), .in_2(B), .out_3(A_B_3));
  tb_or tb_or_1 (.in_1(tb_and_1_out_3), .in_2(tb_and_2_out_3), .out_3(A_B));
endmodule

module _2bit_comparator (
  input  [1:0] B,
  input  [1:0] A,
  output a_b,
  output a_b_2,
  output a_b_3
);

  wire n1bit_comparator_1_a_b, n1bit_comparator_1_a_b_2, n1bit_comparator_1_a_b_3, n1bit_comparator_2_a_b,
       n1bit_comparator_2_a_b_2, n1bit_comparator_2_a_b_3, tb_and_1_out_3, tb_and_2_out_3;

  tb_and tb_and_1 (.in_1(n1bit_comparator_1_a_b), .in_2(n1bit_comparator_2_a_b_3), .out_3(tb_and_1_out_3));
  tb_or tb_or_1 (.in_1(n1bit_comparator_1_a_b_3), .in_2(tb_and_1_out_3), .out_3(a_b_3));
  _1bit_comparator u_1bit_comparator_1 (
    .A(A[1]), .B(B[1]), .A_B(n1bit_comparator_1_a_b), .A_B_2(n1bit_comparator_1_a_b_2),
    .A_B_3(n1bit_comparator_1_a_b_3));
  tb_and tb_and_2 (.in_1(n1bit_comparator_2_a_b_2), .in_2(n1bit_comparator_1_a_b), .out_3(tb_and_2_out_3));
  tb_or tb_or_2 (.in_1(tb_and_2_out_3), .in_2(n1bit_comparator_1_a_b_2), .out_3(a_b_2));
  _1bit_comparator u_1bit_comparator_2 (
    .A(A[0]), .B(B[0]), .A_B(n1bit_comparator_2_a_b), .A_B_2(n1bit_comparator_2_a_b_2),
    .A_B_3(n1bit_comparator_2_a_b_3));
  tb_and tb_and_3 (.in_1(n1bit_comparator_2_a_b), .in_2(n1bit_comparator_1_a_b), .out_3(a_b));
endmodule

module _4_bit_comparator (
  input  [3:0] B,
  input  [3:0] A,
  output A_B,
  output A_B_2,
  output A_B_3
);

  wire n2bit_comparator_1_a_b, n2bit_comparator_1_a_b_2, n2bit_comparator_1_a_b_3, n2bit_comparator_2_a_b,
       n2bit_comparator_2_a_b_2, n2bit_comparator_2_a_b_3, tb_and_1_out_3, tb_and_2_out_3;

  tb_and tb_and_1 (.in_1(n2bit_comparator_2_a_b_2), .in_2(n2bit_comparator_1_a_b), .out_3(tb_and_1_out_3));
  tb_or tb_or_1 (.in_1(tb_and_1_out_3), .in_2(n2bit_comparator_1_a_b_2), .out_3(A_B));
  _2bit_comparator u_2bit_comparator_1 (
    .B(B[3:2]), .A(A[3:2]), .a_b_3(n2bit_comparator_1_a_b_3), .a_b_2(n2bit_comparator_1_a_b_2),
    .a_b(n2bit_comparator_1_a_b));
  tb_and tb_and_2 (.in_1(n2bit_comparator_2_a_b_3), .in_2(n2bit_comparator_1_a_b), .out_3(tb_and_2_out_3));
  tb_or tb_or_2 (.in_1(tb_and_2_out_3), .in_2(n2bit_comparator_1_a_b_3), .out_3(A_B_2));
  _2bit_comparator u_2bit_comparator_2 (
    .B(B[1:0]), .A(A[1:0]), .a_b_3(n2bit_comparator_2_a_b_3), .a_b_2(n2bit_comparator_2_a_b_2),
    .a_b(n2bit_comparator_2_a_b));
  tb_and tb_and_3 (.in_1(n2bit_comparator_2_a_b), .in_2(n2bit_comparator_1_a_b), .out_3(A_B_3));
endmodule
