// Logisim project 2101CS09_3.circ as structural Verilog: 7 circuits, main circuit E1_4_BIT_REGISTER
module E1_4_BIT_REGISTER (
  input  in_1,
  output out
);

  wire cllk_out, d_ff_1_q, d_ff_2_q, d_ff_3_q, d_ff_4_q;

  Clock cllk (.out(cllk_out));
  D_Flip_Flop d_ff_1 (.clk(cllk_out), .D(in_1), .Q(d_ff_1_q));  // open: Qn, preset, en, reset
  D_Flip_Flop d_ff_2 (.clk(cllk_out), .D(d_ff_1_q), .Q(d_ff_2_q));  // open: Qn, preset, en, reset
  D_Flip_Flop d_ff_3 (.clk(cllk_out), .D(d_ff_2_q), .Q(d_ff_3_q));  // open: Qn, preset, en, reset
  D_Flip_Flop d_ff_4 (.clk(cllk_out), .D(d_ff_3_q), .Q(d_ff_4_q));  // open: Qn, preset, en, reset
  D_Flip_Flop d_ff_5 (.clk(cllk_out), .D(d_ff_4_q), .Q(out));  // open: Qn, preset, en, reset
endmodule

module E2_4_BIT_REGISTER (
  input  in_1,
  output out_2,
  output out_3,
  output out_4,
  output out_5
);

  wire clk_out;

  Clock clk (.out(clk_out));
  T_Flip_Flop t_ff_1 (.clk(clk_out), .T(in_1), .Q(out_2));  // open: Qn, preset, reset, en
  T_Flip_Flop t_ff_2 (.clk(out_2), .T(in_1), .Q(out_3));  // open: Qn, preset, reset, en
  T_Flip_Flop t_ff_3 (.clk(out_3), .T(in_1), .Q(out_4));  // open: Qn, preset, reset, en
  Hex_Digit_Display hex_digit_display_1 (.value({out_5, out_4, out_3, out_2}));  // open: dp
  T_Flip_Flop t_ff_4 (.clk(out_4), .T(in_1), .Q(out_5));  // open: Qn, preset, reset, en
endmodule

module E3_5BIT_PARALLEL (
  input  [4:0] Input,
  input  in_2,
  output [4:0] Output
);

  Register #(.width(32)) register_1 ();  // open: D, en, Q, clk, clr
  D_Flip_Flop D__Flipflop (.clk(in_2), .D(Input[0]), .Q(Output[0]));  // open: Qn, preset, en, reset
  D_Flip_Flop D__Flipflop_2 (.clk(in_2), .D(Input[1]), .Q(Output[1]));  // open: Qn, preset, en, reset
  D_Flip_Flop D__Flipflop_3 (.clk(in_2), .D(Input[2]), .Q(Output[2]));  // open: Qn, preset, en, reset
  D_Flip_Flop D__Flipflop_4 (.clk(in_2), .D(Input[3]), .Q(Output[3]));  // open: Qn, preset, en, reset
  D_Flip_Flop D__Flipflop_5 (.clk(in_2), .D(Input[4]), .Q(Output[4]));  // open: Qn, preset, en, reset
endmodule

module E4_4BIT_SHIFT (
  input  shr_in,
  input  shr,
  output Q0,
  output Q1,
  output Q2,
  output Q3
);

  wire CLK_out, multiplexer_1_out, multiplexer_2_out, multiplexer_3_out, multiplexer_4_out, not_1_out;

  Clock CLK (.out(CLK_out));
  not not_1 (not_1_out, shr);
  Multiplexer multiplexer_1 (.in0(shr_in), .in1(Q0), .out(multiplexer_1_out), .sel(not_1_out));  // open: en
  D_Flip_Flop d_ff_1 (.clk(CLK_out), .D(multiplexer_1_out), .Q(Q0));  // open: Qn, preset, en, reset
  Multiplexer multiplexer_2 (.in0(Q0), .in1(Q1), .out(multiplexer_2_out), .sel(not_1_out));  // open: en
  D_Flip_Flop d_ff_2 (.clk(CLK_out), .D(multiplexer_2_out), .Q(Q1));  // open: Qn, preset, en, reset
  Multiplexer multiplexer_3 (.in0(Q1), .in1(Q2), .out(multiplexer_3_out), .sel(not_1_out));  // open: en
  D_Flip_Flop d_ff_3 (.clk(CLK_out), .D(multiplexer_3_out), .Q(Q2));  // open: Qn, preset, en, reset
  Multiplexer multiplexer_4 (.in0(Q2), .in1(Q3), .out(multiplexer_4_out), .sel(not_1_out));  // open: en
  D_Flip_Flop d_ff_4 (.clk(CLK_out), .D(multiplexer_4_out), .Q(Q3));  // open: Qn, preset, en, reset
endmodule

module E5_8X8_REGISTER (
  input  [7:0] Input,
  input  [2:0] Decd,
  input  [2:0] Selection_line,
  output [7:0] out_4
);

  wire clock_1_out, decoder_1_out0, decoder_1_out1, decoder_1_out2, decoder_1_out3, decoder_1_out4,
       decoder_1_out5, decoder_1_out6, decoder_1_out7;
  wire [7:0] d_ff_57_q, d_ff_58_q, d_ff_59_q, d_ff_60_q, d_ff_61_q, d_ff_62_q, d_ff_63_q, d_ff_64_q;

  Decoder #(.select(3)) decoder_1 (
    .out0(decoder_1_out0), .out1(decoder_1_out1), .out2(decoder_1_out2), .out3(decoder_1_out3),
    .out4(decoder_1_out4), .out5(decoder_1_out5), .out6(decoder_1_out6), .out7(decoder_1_out7), .sel(Decd));  // open: en
  Clock clock_1 (.out(clock_1_out));
  D_Flip_Flop d_ff_1 (
    .clk(clock_1_out), .D(Input[7]), .Q(d_ff_57_q[7]), .en(decoder_1_out0));  // open: Qn, preset, reset
  D_Flip_Flop d_ff_2 (
    .clk(clock_1_out), .D(Input[7]), .Q(d_ff_58_q[7]), .en(decoder_1_out1));  // open: Qn, preset, reset
  D_Flip_Flop d_ff_3 (
    .clk(clock_1_out), .D(Input[7]), .Q(d_ff_59_q[7]), .en(decoder_1_out2));  // open: Qn, preset, reset
  D_Flip_Flop d_ff_4 (
    .clk(clock_1_out), .D(Input[7]), .Q(d_ff_60_q[7]), .en(decoder_1_out3));  // open: Qn, preset, reset
  D_Flip_Flop d_ff_5 (
    .clk(clock_1_out), .D(Input[7]), .Q(d_ff_61_q[7]), .en(decoder_1_out4));  // open: Qn, preset, reset
  D_Flip_Flop d_ff_6 (
    .clk(clock_1_out), .D(Input[7]), .Q(d_ff_62_q[7]), .en(decoder_1_out5));  // open: Qn, preset, reset
  D_Flip_Flop d_ff_7 (
    .clk(clock_1_out), .D(Input[7]), .Q(d_ff_63_q[7]), .en(decoder_1_out6));  // open: Qn, preset, reset
  D_Flip_Flop d_ff_8 (
    .clk(clock_1_out), .D(Input[7]), .Q(d_ff_64_q[7]), .en(decoder_1_out7));  // open: Qn, preset, reset
  D_Flip_Flop d_ff_9 (
    .clk(clock_1_out), .D(Input[6]), .Q(d_ff_57_q[6]), .en(decoder_1_out0));  // open: Qn, preset, reset
  D_Flip_Flop d_ff_10 (
    .clk(clock_1_out), .D(Input[6]), .Q(d_ff_58_q[6]), .en(decoder_1_out1));  // open: Qn, preset, reset
  D_Flip_Flop d_ff_11 (
    .clk(clock_1_out), .D(Input[6]), .Q(d_ff_59_q[6]), .en(decoder_1_out2));  // open: Qn, preset, reset
  D_Flip_Flop d_ff_12 (
    .clk(clock_1_out), .D(Input[6]), .Q(d_ff_60_q[6]), .en(decoder_1_out3));  // open: Qn, preset, reset
  D_Flip_Flop d_ff_13 (
    .clk(clock_1_out), .D(Input[6]), .Q(d_ff_61_q[6]), .en(decoder_1_out4));  // open: Qn, preset, reset
  D_Flip_Flop d_ff_14 (
    .clk(clock_1_out), .D(Input[6]), .Q(d_ff_62_q[6]), .en(decoder_1_out5));  // open: Qn, preset, reset
  D_Flip_Flop d_ff_15 (
    .clk(clock_1_out), .D(Input[6]), .Q(d_ff_63_q[6]), .en(decoder_1_out6));  // open: Qn, preset, reset
  D_Flip_Flop d_ff_16 (
    .clk(clock_1_out), .D(Input[6]), .Q(d_ff_64_q[6]), .en(decoder_1_out7));  // open: Qn, preset, reset
  D_Flip_Flop d_ff_17 (
    .clk(clock_1_out), .D(Input[5]), .Q(d_ff_57_q[5]), .en(decoder_1_out0));  // open: Qn, preset, reset
  D_Flip_Flop d_ff_18 (
    .clk(clock_1_out), .D(Input[5]), .Q(d_ff_58_q[5]), .en(decoder_1_out1));  // open: Qn, preset, reset
  D_Flip_Flop d_ff_19 (
    .clk(clock_1_out), .D(Input[5]), .Q(d_ff_59_q[5]), .en(decoder_1_out2));  // open: Qn, preset, reset
  D_Flip_Flop d_ff_20 (
    .clk(clock_1_out), .D(Input[5]), .Q(d_ff_60_q[5]), .en(decoder_1_out3));  // open: Qn, preset, reset
  D_Flip_Flop d_ff_21 (
    .clk(clock_1_out), .D(Input[5]), .Q(d_ff_61_q[5]), .en(decoder_1_out4));  // open: Qn, preset, reset
  D_Flip_Flop d_ff_22 (
    .clk(clock_1_out), .D(Input[5]), .Q(d_ff_62_q[5]), .en(decoder_1_out5));  // open: Qn, preset, reset
  D_Flip_Flop d_ff_23 (
    .clk(clock_1_out), .D(Input[5]), .Q(d_ff_63_q[5]), .en(decoder_1_out6));  // open: Qn, preset, reset
  D_Flip_Flop d_ff_24 (
    .clk(clock_1_out), .D(Input[5]), .Q(d_ff_64_q[5]), .en(decoder_1_out7));  // open: Qn, preset, reset
  D_Flip_Flop d_ff_25 (
    .clk(clock_1_out), .D(Input[4]), .Q(d_ff_57_q[4]), .en(decoder_1_out0));  // open: Qn, preset, reset
  D_Flip_Flop d_ff_26 (
    .clk(clock_1_out), .D(Input[4]), .Q(d_ff_58_q[4]), .en(decoder_1_out1));  // open: Qn, preset, reset
  D_Flip_Flop d_ff_27 (
    .clk(clock_1_out), .D(Input[4]), .Q(d_ff_59_q[4]), .en(decoder_1_out2));  // open: Qn, preset, reset
  D_Flip_Flop d_ff_28 (
    .clk(clock_1_out), .D(Input[4]), .Q(d_ff_60_q[4]), .en(decoder_1_out3));  // open: Qn, preset, reset
  D_Flip_Flop d_ff_29 (
    .clk(clock_1_out), .D(Input[4]), .Q(d_ff_61_q[4]), .en(decoder_1_out4));  // open: Qn, preset, reset
  D_Flip_Flop d_ff_30 (
    .clk(clock_1_out), .D(Input[4]), .Q(d_ff_62_q[4]), .en(decoder_1_out5));  // open: Qn, preset, reset
  D_Flip_Flop d_ff_31 (
    .clk(clock_1_out), .D(Input[4]), .Q(d_ff_63_q[4]), .en(decoder_1_out6));  // open: Qn, preset, reset
  D_Flip_Flop d_ff_32 (
    .clk(clock_1_out), .D(Input[4]), .Q(d_ff_64_q[4]), .en(decoder_1_out7));  // open: Qn, preset, reset
  D_Flip_Flop d_ff_33 (
    .clk(clock_1_out), .D(Input[3]), .Q(d_ff_57_q[3]), .en(decoder_1_out0));  // open: Qn, preset, reset
  D_Flip_Flop d_ff_34 (
    .clk(clock_1_out), .D(Input[3]), .Q(d_ff_58_q[3]), .en(decoder_1_out1));  // open: Qn, preset, reset
  D_Flip_Flop d_ff_35 (
    .clk(clock_1_out), .D(Input[3]), .Q(d_ff_59_q[3]), .en(decoder_1_out2));  // open: Qn, preset, reset
  D_Flip_Flop d_ff_36 (
    .clk(clock_1_out), .D(Input[3]), .Q(d_ff_60_q[3]), .en(decoder_1_out3));  // open: Qn, preset, reset
  D_Flip_Flop d_ff_37 (
    .clk(clock_1_out), .D(Input[3]), .Q(d_ff_61_q[3]), .en(decoder_1_out4));  // open: Qn, preset, reset
  D_Flip_Flop d_ff_38 (
    .clk(clock_1_out), .D(Input[3]), .Q(d_ff_62_q[3]), .en(decoder_1_out5));  // open: Qn, preset, reset
  D_Flip_Flop d_ff_39 (
    .clk(clock_1_out), .D(Input[3]), .Q(d_ff_63_q[3]), .en(decoder_1_out6));  // open: Qn, preset, reset
  D_Flip_Flop d_ff_40 (
    .clk(clock_1_out), .D(Input[3]), .Q(d_ff_64_q[3]), .en(decoder_1_out7));  // open: Qn, preset, reset
  D_Flip_Flop d_ff_41 (
    .clk(clock_1_out), .D(Input[2]), .Q(d_ff_57_q[2]), .en(decoder_1_out0));  // open: Qn, preset, reset
  D_Flip_Flop d_ff_42 (
    .clk(clock_1_out), .D(Input[2]), .Q(d_ff_58_q[2]), .en(decoder_1_out1));  // open: Qn, preset, reset
  D_Flip_Flop d_ff_43 (
    .clk(clock_1_out), .D(Input[2]), .Q(d_ff_59_q[2]), .en(decoder_1_out2));  // open: Qn, preset, reset
  D_Flip_Flop d_ff_44 (
    .clk(clock_1_out), .D(Input[2]), .Q(d_ff_60_q[2]), .en(decoder_1_out3));  // open: Qn, preset, reset
  D_Flip_Flop d_ff_45 (
    .clk(clock_1_out), .D(Input[2]), .Q(d_ff_61_q[2]), .en(decoder_1_out4));  // open: Qn, preset, reset
  D_Flip_Flop d_ff_46 (
    .clk(clock_1_out), .D(Input[2]), .Q(d_ff_62_q[2]), .en(decoder_1_out5));  // open: Qn, preset, reset
  D_Flip_Flop d_ff_47 (
    .clk(clock_1_out), .D(Input[2]), .Q(d_ff_63_q[2]), .en(decoder_1_out6));  // open: Qn, preset, reset
  D_Flip_Flop d_ff_48 (
    .clk(clock_1_out), .D(Input[2]), .Q(d_ff_64_q[2]), .en(decoder_1_out7));  // open: Qn, preset, reset
  D_Flip_Flop d_ff_49 (
    .clk(clock_1_out), .D(Input[1]), .Q(d_ff_57_q[1]), .en(decoder_1_out0));  // open: Qn, preset, reset
  D_Flip_Flop d_ff_50 (
    .clk(clock_1_out), .D(Input[1]), .Q(d_ff_58_q[1]), .en(decoder_1_out1));  // open: Qn, preset, reset
  D_Flip_Flop d_ff_51 (
    .clk(clock_1_out), .D(Input[1]), .Q(d_ff_59_q[1]), .en(decoder_1_out2));  // open: Qn, preset, reset
  D_Flip_Flop d_ff_52 (
    .clk(clock_1_out), .D(Input[1]), .Q(d_ff_60_q[1]), .en(decoder_1_out3));  // open: Qn, preset, reset
  D_Flip_Flop d_ff_53 (
    .clk(clock_1_out), .D(Input[1]), .Q(d_ff_61_q[1]), .en(decoder_1_out4));  // open: Qn, preset, reset
  D_Flip_Flop d_ff_54 (
    .clk(clock_1_out), .D(Input[1]), .Q(d_ff_62_q[1]), .en(decoder_1_out5));  // open: Qn, preset, reset
  D_Flip_Flop d_ff_55 (
    .clk(clock_1_out), .D(Input[1]), .Q(d_ff_63_q[1]), .en(decoder_1_out6));  // open: Qn, preset, reset
  D_Flip_Flop d_ff_56 (
    .clk(clock_1_out), .D(Input[1]), .Q(d_ff_64_q[1]), .en(decoder_1_out7));  // open: Qn, preset, reset
  D_Flip_Flop d_ff_57 (
    .clk(clock_1_out), .D(Input[0]), .Q(d_ff_57_q[0]), .en(decoder_1_out0));  // open: Qn, preset, reset
  D_Flip_Flop d_ff_58 (
    .clk(clock_1_out), .D(Input[0]), .Q(d_ff_58_q[0]), .en(decoder_1_out1));  // open: Qn, preset, reset
  D_Flip_Flop d_ff_59 (
    .clk(clock_1_out), .D(Input[0]), .Q(d_ff_59_q[0]), .en(decoder_1_out2));  // open: Qn, preset, reset
  D_Flip_Flop d_ff_60 (
    .clk(clock_1_out), .D(Input[0]), .Q(d_ff_60_q[0]), .en(decoder_1_out3));  // open: Qn, preset, reset
  D_Flip_Flop d_ff_61 (
    .clk(clock_1_out), .D(Input[0]), .Q(d_ff_61_q[0]), .en(decoder_1_out4));  // open: Qn, preset, reset
  D_Flip_Flop d_ff_62 (
    .clk(clock_1_out), .D(Input[0]), .Q(d_ff_62_q[0]), .en(decoder_1_out5));  // open: Qn, preset, reset
  D_Flip_Flop d_ff_63 (
    .clk(clock_1_out), .D(Input[0]), .Q(d_ff_63_q[0]), .en(decoder_1_out6));  // open: Qn, preset, reset
  D_Flip_Flop d_ff_64 (
    .clk(clock_1_out), .D(Input[0]), .Q(d_ff_64_q[0]), .en(decoder_1_out7));  // open: Qn, preset, reset
  Multiplexer #(.select(3), .width(8)) multiplexer_1 (
    .in0(d_ff_57_q), .in1(d_ff_58_q), .in2(d_ff_59_q), .in3(d_ff_60_q), .in4(d_ff_61_q), .in5(d_ff_62_q),
    .in6(d_ff_63_q), .in7(d_ff_64_q), .out(out_4), .sel(Selection_line));  // open: en

  // Notes on the sheet:
  //   This is for the output , as it gives selection input to the mux thus directs which should be shown as output 
endmodule

module E6_32X32_REGISTER (
  input  [4:0] in_1,
  input  [4:0] in_2,
  input  [4:0] in_3,
  input  [31:0] in_4,
  output [31:0] out_5,
  output [31:0] out_6
);

  wire clock_1_out, decoder_1_out0, decoder_1_out1, decoder_1_out2, decoder_1_out3, decoder_1_out4,
       decoder_1_out5, decoder_1_out6, decoder_1_out7, decoder_1_out8, decoder_1_out9, decoder_1_out10,
       decoder_1_out11, decoder_1_out12, decoder_1_out13, decoder_1_out14, decoder_1_out15, decoder_1_out16,
       decoder_1_out17, decoder_1_out18, decoder_1_out19, decoder_1_out20, decoder_1_out21, decoder_1_out22,
       decoder_1_out23, decoder_1_out24, decoder_1_out25, decoder_1_out26, decoder_1_out27, decoder_1_out28,
       decoder_1_out29, decoder_1_out30, decoder_1_out31, undriven, undriven_2, undriven_3, undriven_4,
       undriven_5, undriven_6, undriven_7, undriven_8, undriven_9, undriven_10, undriven_11, undriven_12,
       undriven_13, undriven_14, undriven_15, undriven_16, undriven_17, undriven_18, undriven_19,
       undriven_20, undriven_21, undriven_22, undriven_23, undriven_24, undriven_25, undriven_26,
       undriven_27, undriven_28, undriven_29, undriven_30, undriven_31, undriven_32;
  wire [31:0] register_1_q, register_2_q, register_3_q, register_4_q, register_5_q, register_6_q,
       register_7_q, register_8_q, register_9_q, register_10_q, register_11_q, register_12_q, register_13_q,
       register_14_q, register_15_q, register_16_q, register_17_q, register_18_q, register_19_q,
       register_20_q, register_21_q, register_22_q, register_23_q, register_24_q, register_25_q,
       register_26_q, register_27_q, register_28_q, register_29_q, register_30_q, register_31_q,
       register_32_q;

  Decoder #(.select(5)) decoder_1 (
    .out0(decoder_1_out0), .out1(decoder_1_out1), .out2(decoder_1_out2), .out3(decoder_1_out3),
    .out4(decoder_1_out4), .out5(decoder_1_out5), .out6(decoder_1_out6), .out7(decoder_1_out7),
    .out8(decoder_1_out8), .out9(decoder_1_out9), .out10(decoder_1_out10), .out11(decoder_1_out11),
    .out12(decoder_1_out12), .out13(decoder_1_out13), .out14(decoder_1_out14), .out15(decoder_1_out15),
    .out16(decoder_1_out16), .out17(decoder_1_out17), .out18(decoder_1_out18), .out19(decoder_1_out19),
    .out20(decoder_1_out20), .out21(decoder_1_out21), .out22(decoder_1_out22), .out23(decoder_1_out23),
    .out24(decoder_1_out24), .out25(decoder_1_out25), .out26(decoder_1_out26), .out27(decoder_1_out27),
    .out28(decoder_1_out28), .out29(decoder_1_out29), .out30(decoder_1_out30), .out31(decoder_1_out31),
    .sel(in_2));  // open: en
  Clock clock_1 (.out(clock_1_out));
  Register #(.width(32)) register_1 (
    .D(in_4), .en(decoder_1_out0), .Q(register_1_q), .clk(clock_1_out), .clr(undriven));
  Register #(.width(32)) register_2 (
    .D(in_4), .en(decoder_1_out1), .Q(register_2_q), .clk(clock_1_out), .clr(undriven_2));
  Register #(.width(32)) register_3 (
    .D(in_4), .en(decoder_1_out2), .Q(register_3_q), .clk(clock_1_out), .clr(undriven_3));
  Register #(.width(32)) register_4 (
    .D(in_4), .en(decoder_1_out3), .Q(register_4_q), .clk(clock_1_out), .clr(undriven_4));
  Register #(.width(32)) register_5 (
    .D(in_4), .en(decoder_1_out4), .Q(register_5_q), .clk(clock_1_out), .clr(undriven_5));
  Register #(.width(32)) register_6 (
    .D(in_4), .en(decoder_1_out5), .Q(register_6_q), .clk(clock_1_out), .clr(undriven_6));
  Register #(.width(32)) register_7 (
    .D(in_4), .en(decoder_1_out6), .Q(register_7_q), .clk(clock_1_out), .clr(undriven_7));
  Register #(.width(32)) register_8 (
    .D(in_4), .en(decoder_1_out7), .Q(register_8_q), .clk(clock_1_out), .clr(undriven_8));
  Register #(.width(32)) register_9 (
    .D(in_4), .en(decoder_1_out8), .Q(register_9_q), .clk(clock_1_out), .clr(undriven_9));
  Register #(.width(32)) register_10 (
    .D(in_4), .en(decoder_1_out9), .Q(register_10_q), .clk(clock_1_out), .clr(undriven_10));
  Register #(.width(32)) register_11 (
    .D(in_4), .en(decoder_1_out10), .Q(register_11_q), .clk(clock_1_out), .clr(undriven_11));
  Register #(.width(32)) register_12 (
    .D(in_4), .en(decoder_1_out11), .Q(register_12_q), .clk(clock_1_out), .clr(undriven_12));
  Register #(.width(32)) register_13 (
    .D(in_4), .en(decoder_1_out12), .Q(register_13_q), .clk(clock_1_out), .clr(undriven_13));
  Register #(.width(32)) register_14 (
    .D(in_4), .en(decoder_1_out13), .Q(register_14_q), .clk(clock_1_out), .clr(undriven_14));
  Register #(.width(32)) register_15 (
    .D(in_4), .en(decoder_1_out14), .Q(register_15_q), .clk(clock_1_out), .clr(undriven_15));
  Register #(.width(32)) register_16 (
    .D(in_4), .en(decoder_1_out15), .Q(register_16_q), .clk(clock_1_out), .clr(undriven_16));
  Register #(.width(32)) register_17 (
    .D(in_4), .en(decoder_1_out16), .Q(register_17_q), .clk(clock_1_out), .clr(undriven_17));
  Register #(.width(32)) register_18 (
    .D(in_4), .en(decoder_1_out17), .Q(register_18_q), .clk(clock_1_out), .clr(undriven_18));
  Register #(.width(32)) register_19 (
    .D(in_4), .en(decoder_1_out18), .Q(register_19_q), .clk(clock_1_out), .clr(undriven_19));
  Register #(.width(32)) register_20 (
    .D(in_4), .en(decoder_1_out19), .Q(register_20_q), .clk(clock_1_out), .clr(undriven_20));
  Register #(.width(32)) register_21 (
    .D(in_4), .en(decoder_1_out20), .Q(register_21_q), .clk(clock_1_out), .clr(undriven_21));
  Register #(.width(32)) register_22 (
    .D(in_4), .en(decoder_1_out21), .Q(register_22_q), .clk(clock_1_out), .clr(undriven_22));
  Register #(.width(32)) register_23 (
    .D(in_4), .en(decoder_1_out22), .Q(register_23_q), .clk(clock_1_out), .clr(undriven_23));
  Register #(.width(32)) register_24 (
    .D(in_4), .en(decoder_1_out23), .Q(register_24_q), .clk(clock_1_out), .clr(undriven_24));
  Register #(.width(32)) register_25 (
    .D(in_4), .en(decoder_1_out24), .Q(register_25_q), .clk(clock_1_out), .clr(undriven_25));
  Register #(.width(32)) register_26 (
    .D(in_4), .en(decoder_1_out25), .Q(register_26_q), .clk(clock_1_out), .clr(undriven_26));
  Register #(.width(32)) register_27 (
    .D(in_4), .en(decoder_1_out26), .Q(register_27_q), .clk(clock_1_out), .clr(undriven_27));
  Register #(.width(32)) register_28 (
    .D(in_4), .en(decoder_1_out27), .Q(register_28_q), .clk(clock_1_out), .clr(undriven_28));
  Register #(.width(32)) register_29 (
    .D(in_4), .en(decoder_1_out28), .Q(register_29_q), .clk(clock_1_out), .clr(undriven_29));
  Register #(.width(32)) register_30 (
    .D(in_4), .en(decoder_1_out29), .Q(register_30_q), .clk(clock_1_out), .clr(undriven_30));
  Register #(.width(32)) register_31 (
    .D(in_4), .en(decoder_1_out30), .Q(register_31_q), .clk(clock_1_out), .clr(undriven_31));
  Register #(.width(32)) register_32 (
    .D(in_4), .en(decoder_1_out31), .Q(register_32_q), .clk(clock_1_out), .clr(undriven_32));
  Multiplexer #(.select(5), .width(32)) multiplexer_1 (
    .in0(register_1_q), .in1(register_2_q), .in2(register_3_q), .in3(register_4_q), .in4(register_5_q),
    .in5(register_6_q), .in6(register_7_q), .in7(register_8_q), .in8(register_9_q), .in9(register_10_q),
    .in10(register_11_q), .in11(register_12_q), .in12(register_13_q), .in13(register_14_q),
    .in14(register_15_q), .in15(register_16_q), .in16(register_17_q), .in17(register_18_q),
    .in18(register_19_q), .in19(register_20_q), .in20(register_21_q), .in21(register_22_q),
    .in22(register_23_q), .in23(register_24_q), .in24(register_25_q), .in25(register_26_q),
    .in26(register_27_q), .in27(register_28_q), .in28(register_29_q), .in29(register_30_q),
    .in30(register_31_q), .in31(register_32_q), .out(out_5), .sel(in_1));  // open: en
  Multiplexer #(.select(5), .width(32)) multiplexer_2 (
    .in0(register_1_q), .in1(register_2_q), .in2(register_3_q), .in3(register_4_q), .in4(register_5_q),
    .in5(register_6_q), .in6(register_7_q), .in7(register_8_q), .in8(register_9_q), .in9(register_10_q),
    .in10(register_11_q), .in11(register_12_q), .in12(register_13_q), .in13(register_14_q),
    .in14(register_15_q), .in15(register_16_q), .in16(register_17_q), .in17(register_18_q),
    .in18(register_19_q), .in19(register_20_q), .in20(register_21_q), .in21(register_22_q),
    .in22(register_23_q), .in23(register_24_q), .in24(register_25_q), .in25(register_26_q),
    .in26(register_27_q), .in27(register_28_q), .in28(register_29_q), .in29(register_30_q),
    .in30(register_31_q), .in31(register_32_q), .out(out_6), .sel(in_3));  // open: en

  // Notes on the sheet:
  //   Selector for Decoder
  //   32 bit Decoder
  //   Input
  //   Clock
  //   32 bit registor
  //   Multiplexer
  //   Multiplexer
  //   Output 1
  //   Selector for MUX
  //   Output 2
  //   Selector for MUX
endmodule

module E7_TEMPERATURE_AVG (
  input  [6:0] in_1,
  output [6:0] out_2,
  output [6:0] out_3
);

  wire clock_1_out;
  wire [1:0] adder_2_out;
  wire [6:0] adder_1_out, adder_3_out, register_1_q, register_2_q, register_3_q, register_4_q;

  Clock clock_1 (.out(clock_1_out));
  Register #(.width(7)) register_1 (.D(in_1), .en(1'b1), .Q(register_1_q), .clk(clock_1_out), .clr(1'b0));
  Register #(.width(7)) register_2 (.D(register_1_q), .en(1'b1), .Q(register_2_q), .clk(clock_1_out), .clr(1'b0));
  Register #(.width(7)) register_3 (.D(register_2_q), .en(1'b1), .Q(register_3_q), .clk(clock_1_out), .clr(1'b0));
  Adder #(.width(7)) adder_1 (.a(register_1_q), .b(register_2_q), .out(adder_1_out));  // open: cin, cout
  Register #(.width(7)) register_4 (.D(register_3_q), .en(1'b1), .Q(register_4_q), .clk(clock_1_out), .clr(1'b0));
  Adder #(.width(7)) adder_2 (.a(adder_1_out), .b(adder_3_out), .out({out_3[4:0], adder_2_out}));  // open: cin, cout
  Register #(.width(7)) register_5 (.D({2'b00, out_3[4:0]}), .en(1'b1), .Q(out_2), .clk(clock_1_out), .clr(1'b0));
  Adder #(.width(7)) adder_3 (.a(register_4_q), .b(register_3_q), .out(adder_3_out));  // open: cin, cout

  assign out_3[6:5] = 2'b00;
endmodule
