// Logisim project 2101CS09_4.circ as structural Verilog: 7 circuits, main circuit Right Shifter
module Right_Shifter (
  input  [3:0] Shift_Amount,
  input  [14:0] Input,
  output [14:0] Output
);

  wire or_1_out, or_2_out, or_3_out, or_4_out, or_5_out, or_6_out, or_7_out, or_8_out, or_9_out, or_10_out,
       or_11_out, or_12_out, or_13_out, or_14_out;

  Multiplexer #(.select(4), .disabled(0), .enable("false")) multiplexer_1 (
    .in0(Input[14]), .in1(1'b0), .in2(1'b0), .in3(1'b0), .in4(1'b0), .in5(1'b0), .in6(1'b0), .in7(1'b0),
    .in8(1'b0), .in9(1'b0), .in10(1'b0), .in11(1'b0), .in12(1'b0), .in13(1'b0), .in14(1'b0), .in15(1'b0),
    .out(Output[14]), .sel(Shift_Amount));
  Multiplexer #(.select(4), .disabled(0), .enable("false")) multiplexer_2 (
    .in0(Input[13]), .in1(Input[14]), .in2(1'b0), .in3(1'b0), .in4(1'b0), .in5(1'b0), .in6(1'b0), .in7(1'b0),
    .in8(1'b0), .in9(1'b0), .in10(1'b0), .in11(1'b0), .in12(1'b0), .in13(1'b0), .in14(1'b0), .in15(1'b0),
    .out(Output[13]), .sel(Shift_Amount));
  Multiplexer #(.select(4), .disabled(0), .enable("false")) multiplexer_3 (
    .in0(Input[12]), .in1(Input[13]), .in2(Input[14]), .in3(1'b0), .in4(1'b0), .in5(1'b0), .in6(1'b0),
    .in7(1'b0), .in8(1'b0), .in9(1'b0), .in10(1'b0), .in11(1'b0), .in12(1'b0), .in13(1'b0), .in14(1'b0),
    .in15(1'b0), .out(Output[12]), .sel(Shift_Amount));
  Multiplexer #(.select(4), .disabled(0), .enable("false")) multiplexer_4 (
    .in0(Input[11]), .in1(Input[12]), .in2(Input[13]), .in3(Input[14]), .in4(1'b0), .in5(1'b0), .in6(1'b0),
    .in7(1'b0), .in8(1'b0), .in9(1'b0), .in10(1'b0), .in11(1'b0), .in12(1'b0), .in13(1'b0), .in14(1'b0),
    .in15(1'b0), .out(Output[11]), .sel(Shift_Amount));
  Multiplexer #(.select(4), .disabled(0), .enable("false")) multiplexer_5 (
    .in0(Input[10]), .in1(Input[11]), .in2(Input[12]), .in3(Input[13]), .in4(Input[14]), .in5(1'b0),
    .in6(1'b0), .in7(1'b0), .in8(1'b0), .in9(1'b0), .in10(1'b0), .in11(1'b0), .in12(1'b0), .in13(1'b0),
    .in14(1'b0), .in15(1'b0), .out(Output[10]), .sel(Shift_Amount));
  Multiplexer #(.select(4), .disabled(0), .enable("false")) multiplexer_6 (
    .in0(Input[9]), .in1(Input[10]), .in2(Input[11]), .in3(Input[12]), .in4(Input[13]), .in5(Input[14]),
    .in6(1'b0), .in7(1'b0), .in8(1'b0), .in9(1'b0), .in10(1'b0), .in11(1'b0), .in12(1'b0), .in13(1'b0),
    .in14(1'b0), .in15(1'b0), .out(Output[9]), .sel(Shift_Amount));
  Multiplexer #(.select(4), .disabled(0), .enable("false")) multiplexer_7 (
    .in0(Input[8]), .in1(Input[9]), .in2(Input[10]), .in3(Input[11]), .in4(Input[12]), .in5(Input[13]),
    .in6(Input[14]), .in7(1'b0), .in8(1'b0), .in9(1'b0), .in10(1'b0), .in11(1'b0), .in12(1'b0), .in13(1'b0),
    .in14(1'b0), .in15(1'b0), .out(Output[8]), .sel(Shift_Amount));
  Multiplexer #(.select(4), .disabled(0), .enable("false")) multiplexer_8 (
    .in0(Input[7]), .in1(Input[8]), .in2(Input[9]), .in3(Input[10]), .in4(Input[11]), .in5(Input[12]),
    .in6(Input[13]), .in7(Input[14]), .in8(1'b0), .in9(1'b0), .in10(1'b0), .in11(1'b0), .in12(1'b0),
    .in13(1'b0), .in14(1'b0), .in15(1'b0), .out(Output[7]), .sel(Shift_Amount));
  Multiplexer #(.select(4), .disabled(0), .enable("false")) multiplexer_9 (
    .in0(Input[6]), .in1(Input[7]), .in2(Input[8]), .in3(Input[9]), .in4(Input[10]), .in5(Input[11]),
    .in6(Input[12]), .in7(Input[13]), .in8(Input[14]), .in9(1'b0), .in10(1'b0), .in11(1'b0), .in12(1'b0),
    .in13(1'b0), .in14(1'b0), .in15(1'b0), .out(Output[6]), .sel(Shift_Amount));
  Multiplexer #(.select(4), .disabled(0), .enable("false")) multiplexer_10 (
    .in0(Input[5]), .in1(Input[6]), .in2(Input[7]), .in3(Input[8]), .in4(Input[9]), .in5(Input[10]),
    .in6(Input[11]), .in7(Input[12]), .in8(Input[13]), .in9(Input[14]), .in10(1'b0), .in11(1'b0),
    .in12(1'b0), .in13(1'b0), .in14(1'b0), .in15(1'b0), .out(Output[5]), .sel(Shift_Amount));
  Multiplexer #(.select(4), .disabled(0), .enable("false")) multiplexer_11 (
    .in0(Input[4]), .in1(Input[5]), .in2(Input[6]), .in3(Input[7]), .in4(Input[8]), .in5(Input[9]),
    .in6(Input[10]), .in7(Input[11]), .in8(Input[12]), .in9(Input[13]), .in10(Input[14]), .in11(1'b0),
    .in12(1'b0), .in13(1'b0), .in14(1'b0), .in15(1'b0), .out(Output[4]), .sel(Shift_Amount));
  Multiplexer #(.select(4), .disabled(0), .enable("false")) multiplexer_12 (
    .in0(Input[3]), .in1(Input[4]), .in2(Input[5]), .in3(Input[6]), .in4(Input[7]), .in5(Input[8]),
    .in6(Input[9]), .in7(Input[10]), .in8(Input[11]), .in9(Input[12]), .in10(Input[13]), .in11(Input[14]),
    .in12(1'b0), .in13(1'b0), .in14(1'b0), .in15(1'b0), .out(Output[3]), .sel(Shift_Amount));
  Multiplexer #(.select(4), .disabled(0), .enable("false")) multiplexer_13 (
    .in0(Input[2]), .in1(Input[3]), .in2(Input[4]), .in3(Input[5]), .in4(Input[6]), .in5(Input[7]),
    .in6(Input[8]), .in7(Input[9]), .in8(Input[10]), .in9(Input[11]), .in10(Input[12]), .in11(Input[13]),
    .in12(Input[14]), .in13(1'b0), .in14(1'b0), .in15(1'b0), .out(Output[2]), .sel(Shift_Amount));
  Multiplexer #(.select(4), .disabled(0), .enable("false")) multiplexer_14 (
    .in0(Input[1]), .in1(Input[2]), .in2(Input[3]), .in3(Input[4]), .in4(Input[5]), .in5(Input[6]),
    .in6(Input[7]), .in7(Input[8]), .in8(Input[9]), .in9(Input[10]), .in10(Input[11]), .in11(Input[12]),
    .in12(Input[13]), .in13(Input[14]), .in14(1'b0), .in15(1'b0), .out(Output[1]), .sel(Shift_Amount));
  or or_1 (or_1_out, Input[0], Input[1]);
  or or_2 (or_2_out, or_1_out, Input[2]);
  or or_3 (or_3_out, or_2_out, Input[3]);
  or or_4 (or_4_out, or_3_out, Input[4]);
  or or_5 (or_5_out, or_4_out, Input[5]);
  or or_6 (or_6_out, or_5_out, Input[6]);
  or or_7 (or_7_out, or_6_out, Input[7]);
  or or_8 (or_8_out, or_7_out, Input[8]);
  or or_9 (or_9_out, or_8_out, Input[9]);
  or or_10 (or_10_out, or_9_out, Input[10]);
  or or_11 (or_11_out, or_10_out, Input[11]);
  or or_12 (or_12_out, or_11_out, Input[12]);
  or or_13 (or_13_out, or_12_out, Input[13]);
  or or_14 (or_14_out, or_13_out, Input[14]);
  Multiplexer #(.select(4), .disabled(0), .enable("false")) multiplexer_15 (
    .in0(Input[0]), .in1(or_1_out), .in2(or_2_out), .in3(or_3_out), .in4(or_4_out), .in5(or_5_out),
    .in6(or_6_out), .in7(or_7_out), .in8(or_8_out), .in9(or_9_out), .in10(or_10_out), .in11(or_11_out),
    .in12(or_12_out), .in13(or_13_out), .in14(or_14_out), .in15(1'b0), .out(Output[0]), .sel(Shift_Amount));
endmodule

module Bit_inverter (
  input  Control,
  input  [14:0] Input,
  output [15:0] Output
);

  wire [15:0] xor_1_out;

  assign xor_1_out = {16{Control}} ^ {1'b0, Input};  // XOR_Gate xor_1, 16 bits wide
  Adder #(.width(16)) adder_1 (.a({16{1'b0}}), .b(xor_1_out), .out(Output), .cin(Control));  // open: cout
endmodule

module Bit_Finder (
  input  [15:0] Input,
  output [3:0] Position,
  output Present
);

  wire [3:0] bitfinder_1_index;

  BitFinder #(.width(16)) bitfinder_1 (
    .in({Input[0], Input[1], Input[2], Input[3], Input[4], Input[5], Input[6], Input[7], Input[8], Input[9], Input[10], Input[11], Input[12], Input[13], Input[14], Input[15]}),
    .index(bitfinder_1_index), .found(Present));
  Subtractor #(.width(4)) subtractor_1 (.a(bitfinder_1_index), .b(4'b0000), .out(Position), .bin(1'b1));  // open: bout
endmodule

module Shifter (
  input  [15:0] Input,
  input  [3:0] Shift_Amount,
  output [15:0] Output
);

  wire [15:0] shifter_1_out;

  Shifter_part #(.width(16), .shift("rl")) shifter_1 (
    .in(Input), .\dist (Shift_Amount), .out({shifter_1_out[15], Output[14:1], shifter_1_out[0]}));
  or or_1 (Output[0], shifter_1_out[0], shifter_1_out[15]);

  assign Output[15] = 1'b0;
endmodule

// NORMALIZE
module NORMALISE (
  input  [3:0] Exponent_In,
  input  [15:0] Significant_In,
  output [3:0] Exponent_Out,
  output [15:0] Significant_Out
);

  wire and_1_out, bit_finder_1_p3, nand_1_out, nand_2_out, nor_1_out, or_1_out, subtractor_1_bout;
  wire [3:0] bit_finder_1_p2, multiplexer_2_out, subtractor_1_out, subtractor_2_out;
  wire [15:0] shifter_1_output;

  Multiplexer #(.width(4), .disabled(0), .enable("false")) multiplexer_1 (
    .in0(subtractor_1_out), .in1(4'b0000), .out(Exponent_Out), .sel(and_1_out));
  Subtractor #(.width(4)) subtractor_1 (
    .a(Exponent_In), .b(bit_finder_1_p2), .out(subtractor_1_out), .bin(1'b0), .bout(subtractor_1_bout));
  nor nor_1 (nor_1_out, subtractor_1_out[0], subtractor_1_out[1], subtractor_1_out[2], subtractor_1_out[3]);
  or or_1 (or_1_out, subtractor_1_bout, nor_1_out);
  nand nand_1 (nand_1_out, bit_finder_1_p2[0], bit_finder_1_p2[1], bit_finder_1_p2[2], bit_finder_1_p2[3], bit_finder_1_p3);
  // Bit_Finder bit_finder_1: pin names not known; wires that end beside it: Significant_In, bit_finder_1_p2, bit_finder_1_p3
  and and_1 (and_1_out, or_1_out, nand_1_out);
  nand nand_2 (nand_2_out, Exponent_Out[0], Exponent_Out[1], Exponent_Out[2], Exponent_Out[3]);
  Subtractor #(.width(4)) subtractor_2 (
    .a(Exponent_In), .b(4'b0000), .out(subtractor_2_out), .bin(1'b1));  // open: bout
  Multiplexer #(.width(4), .disabled(0), .enable("false")) multiplexer_2 (
    .in0(bit_finder_1_p2), .in1(subtractor_2_out), .out(multiplexer_2_out), .sel(and_1_out));
  Shifter shifter_1 (.Input(Significant_In), .Shift_Amount(multiplexer_2_out), .Output(shifter_1_output));
  Multiplexer #(.width(16), .disabled(0), .enable("false")) multiplexer_3 (
    .in0(16'h4000), .in1(shifter_1_output), .out(Significant_Out), .sel(nand_2_out));
endmodule

module MINIMUM_COMPARATOR (
  input  [10:0] Fraction_A,
  input  [3:0] Exponent_A,
  input  [10:0] Fraction_B,
  input  [3:0] Exponent_B,
  output [3:0] Exponent_Difference,
  output Number_A___Number_B
);

  wire nor_1_out, nor_2_out, subtractor_1_bout;
  wire [0:0] multiplexer_1_out, multiplexer_2_out;
  wire [3:0] negator_1_out, subtractor_1_out;

  nor nor_1 (nor_1_out, Exponent_A[0], Exponent_A[1], Exponent_A[2], Exponent_A[3]);
  Multiplexer #(.disabled(0), .enable("false")) multiplexer_1 (
    .in0(Exponent_A[0]), .in1(nor_1_out), .out(multiplexer_1_out[0]), .sel(nor_1_out));
  Multiplexer #(.disabled(0), .enable("false")) multiplexer_2 (
    .in0(Exponent_B[0]), .in1(nor_2_out), .out(multiplexer_2_out[0]), .sel(nor_2_out));
  nor nor_2 (nor_2_out, Exponent_B[3], Exponent_B[2], Exponent_B[1], Exponent_B[0]);
  Comparator #(.width(15), .mode("unsigned")) comparator_1 (
    .a({Exponent_A, Fraction_A}), .b({Exponent_B, Fraction_B}), .lt(Number_A___Number_B));  // open: gt, eq
  Subtractor #(.width(4)) subtractor_1 (
    .a({Exponent_A[3:1], multiplexer_1_out[0]}), .b({Exponent_B[3:1], multiplexer_2_out[0]}),
    .out(subtractor_1_out), .bin(1'b0), .bout(subtractor_1_bout));
  Negator #(.width(4)) negator_1 (.in(subtractor_1_out), .out(negator_1_out));
  Multiplexer #(.width(4), .disabled(0), .enable("false")) multiplexer_3 (
    .in0(subtractor_1_out), .in1(negator_1_out), .out(Exponent_Difference), .sel(subtractor_1_bout));
endmodule

module test_float (
  input  SEL,
  input  [15:0] Number_A,
  input  [15:0] Number_B,
  output [15:0] OUTPUT
);

  wire and_1_out, or_2_out, or_4_out, xor_1_out, xor_2_out, xor_4_out;
  wire [1:0] and_2_out, or_5_out, shifter_1_out;
  wire [3:0] adder_1_out, minimum_comparator_1_exponent_difference, multiplexer_1_out, multiplexer_3_out,
       multiplexer_4_out, multiplexer_5_out, multiplexer_8_out, normalise_1_exponent_out;
  wire [12:0] adder_2_out;
  wire [14:0] multiplexer_7_out, multiplexer_9_out, right_shifter_1_output;
  wire [14:14] or_1_out, or_3_out;
  wire [15:0] adder_3_out, bit_extender_1_out, bit_inverter_1_output, multiplexer_2_out, multiplexer_10_out,
       multiplexer_11_out, multiplexer_12_out, normalise_1_significant_out;
  wire [15:15] xor_3_out;

  xor xor_1 (xor_1_out, Number_B[15], SEL);
  Multiplexer #(.width(4), .disabled(0), .enable("false")) multiplexer_1 (
    .in0(4'b0001), .in1(Number_A[14:11]), .out(multiplexer_1_out), .sel(or_1_out[14]));
  ExactlyOne xor_2 (.out(xor_2_out), .in0(Number_B[15]), .in1(Number_A[15]), .in2(SEL));
  Multiplexer #(.disabled(0), .enable("false")) multiplexer_2 (
    .in0(Number_A[15]), .in1(xor_1_out), .out(multiplexer_2_out[15]), .sel(xor_2_out));
  or or_1 (or_1_out[14], Number_A[14], Number_A[13], Number_A[12], Number_A[11]);
  Multiplexer #(.width(4), .disabled(0), .enable("false")) multiplexer_3 (
    .in0(multiplexer_1_out), .in1(multiplexer_8_out), .out(multiplexer_3_out), .sel(xor_2_out));
  Multiplexer #(.width(4), .disabled(0), .enable("false")) multiplexer_4 (
    .in0(4'b0000), .in1(normalise_1_exponent_out), .out(multiplexer_4_out), .sel(adder_2_out[11]));
  Multiplexer #(.width(4), .disabled(0), .enable("false")) multiplexer_5 (
    .in0(multiplexer_4_out), .in1(adder_1_out), .out(multiplexer_5_out), .sel(adder_2_out[12]));
  Adder #(.width(4)) adder_1 (.a(normalise_1_exponent_out), .b(4'b0000), .out(adder_1_out), .cin(1'b1));  // open: cout
  MINIMUM_COMPARATOR minimum_comparator_1 (
    .Fraction_A(Number_A[10:0]), .Exponent_A(Number_A[14:11]), .Fraction_B(Number_B[10:0]),
    .Exponent_B(Number_B[14:11]), .Exponent_Difference(minimum_comparator_1_exponent_difference),
    .Number_A___Number_B(xor_2_out));
  NORMALISE normalise_1 (
    .Exponent_In(multiplexer_3_out), .Significant_In(adder_3_out), .Exponent_Out(normalise_1_exponent_out),
    .Significant_Out(normalise_1_significant_out));
  Multiplexer #(.width(16), .disabled(0), .enable("false")) multiplexer_6 (
    .in0({multiplexer_2_out[15], multiplexer_5_out, multiplexer_2_out[10:0]}), .in1(multiplexer_10_out),
    .out(OUTPUT), .sel(or_4_out));
  Multiplexer #(.width(15), .disabled(0), .enable("false")) multiplexer_7 (
    .in0({or_1_out[14], Number_A[10:0], 3'b000}), .in1({or_3_out[14], Number_B[10:0], 3'b000}),
    .out(multiplexer_7_out), .sel(xor_2_out));
  or or_2 (or_2_out, normalise_1_significant_out[2], normalise_1_significant_out[0]);
  and and_1 (and_1_out, normalise_1_significant_out[1], or_2_out);
  Adder #(.width(13)) adder_2 (
    .a(normalise_1_significant_out[15:3]), .b({13{1'b0}}), .out(adder_2_out), .cin(and_1_out));  // open: cout
  Shifter_part #(.width(13), .shift("lr")) shifter_1 (
    .in(adder_2_out), .\dist ({3'b000, adder_2_out[12]}), .out({shifter_1_out, multiplexer_2_out[10:0]}));
  Multiplexer #(.width(4), .disabled(0), .enable("false")) multiplexer_8 (
    .in0(4'b0001), .in1(Number_B[14:11]), .out(multiplexer_8_out), .sel(or_3_out[14]));
  assign bit_extender_1_out = {{1{1'b0}}, multiplexer_7_out};  // Bit_Extender bit_extender_1
  or or_3 (or_3_out[14], Number_B[14], Number_B[13], Number_B[12], Number_B[11]);
  Multiplexer #(.width(15), .disabled(0), .enable("false")) multiplexer_9 (
    .in0({or_3_out[14], Number_B[10:0], 3'b000}), .in1({or_1_out[14], Number_A[10:0], 3'b000}),
    .out(multiplexer_9_out), .sel(xor_2_out));
  Right_Shifter right_shifter_1 (
    .Shift_Amount(minimum_comparator_1_exponent_difference), .Input(multiplexer_9_out),
    .Output(right_shifter_1_output));
  Bit_inverter bit_inverter_1 (.Control(xor_2_out), .Input(right_shifter_1_output), .Output(bit_inverter_1_output));
  Adder #(.width(16)) adder_3 (
    .a(bit_inverter_1_output), .b(bit_extender_1_out), .out(adder_3_out), .cin(1'b0));  // open: cout
  or or_4 (or_4_out, and_2_out[0], and_2_out[1]);
  and and_2 (and_2_out[0], Number_A[14], Number_A[13], Number_A[12], Number_A[11]);
  or or_5 (or_5_out[0], Number_A[10], Number_A[9], Number_A[8], Number_A[7], Number_A[6], Number_A[5], Number_A[4], Number_A[3], Number_A[2], Number_A[1], Number_A[0]);
  xor xor_3 (xor_3_out[15], SEL, Number_B[15]);
  and and_3 (and_2_out[1], Number_B[14], Number_B[13], Number_B[12], Number_B[11]);
  Multiplexer #(.select(2), .width(16), .disabled(0), .enable("false")) multiplexer_10 (
    .in0(Number_A), .in1(Number_A), .in2({xor_3_out[15], Number_B[14:0]}), .in3(multiplexer_11_out),
    .out(multiplexer_10_out), .sel(and_2_out));
  xor xor_4 (xor_4_out, xor_3_out[15], Number_A[15]);
  Multiplexer #(.select(2), .width(16), .disabled(0), .enable("false")) multiplexer_11 (
    .in0(multiplexer_12_out), .in1(Number_A), .in2({xor_3_out[15], Number_B[14:0]}), .in3(Number_A),
    .out(multiplexer_11_out), .sel(or_5_out));
  or or_6 (or_5_out[1], Number_B[10], Number_B[9], Number_B[8], Number_B[7], Number_B[6], Number_B[5], Number_B[4], Number_B[3], Number_B[2], Number_B[1], Number_B[0]);
  Multiplexer #(.width(16), .disabled(0), .enable("false")) multiplexer_12 (
    .in0({xor_3_out[15], Number_B[14:0]}), .in1({16{1'b1}}), .out(multiplexer_12_out), .sel(xor_4_out));
endmodule
