// Logisim project 2101CS09_Lab- 8.circ as structural Verilog: 13 circuits, main circuit main
module main (
  input  Clear_PC
);

  wire alu_1_zero_bit, and_1_out, clock_1_out, control_1_alusrc, control_1_branch, control_1_jal,
       control_1_jump, control_1_memtoreg, control_1_memwrite, control_1_regwrite;
  wire [1:0] undriven;
  wire [2:0] control_1_aluop;
  wire [4:0] instruction_splitter_1_reg_read_rd, instruction_splitter_1_reg_read_rs,
       instruction_splitter_1_reg_read_rt, multiplexer_4_out;
  wire [5:0] instruction_splitter_1_function, instruction_splitter_1_opcode;
  wire [15:0] instruction_splitter_1_constant_address;
  wire [23:0] shifter_2_out, shifter_4_out;
  wire [25:0] instruction_splitter_1_address, shifter_1_out;
  wire [31:0] adder_1_out, adder_2_out, alu_1_out_6, bit_extender_1_out, bit_extender_2_out,
       multiplexer_1_out, multiplexer_2_out, multiplexer_3_out, multiplexer_5_out, multiplexer_6_out,
       ram_1_data, reg32_1_value_0, reg32_1_value_1, register_1_q, rom_1_data, shifter_3_out;

  Multiplexer #(.width(32), .enable("false")) multiplexer_1 (
    .in0(adder_1_out), .in1(adder_2_out), .out(multiplexer_1_out), .sel(and_1_out));
  Multiplexer #(.width(32), .enable("false")) multiplexer_2 (
    .in0(multiplexer_1_out), .in1(bit_extender_1_out), .out(multiplexer_2_out), .sel(control_1_jump));
  Clock clock_1 (.out(clock_1_out));
  Register #(.width(32)) register_1 (
    .D(multiplexer_2_out), .Q(register_1_q), .clk(clock_1_out), .clr(Clear_PC));  // open: en
  Shifter #(.width(26)) shifter_1 (.in(instruction_splitter_1_address), .\dist (5'b00010), .out(shifter_1_out));
  Shifter #(.width(24), .shift("lr")) shifter_2 (.in(register_1_q[23:0]), .\dist (5'b00010), .out(shifter_2_out));
  Adder #(.width(32)) adder_1 (.a(register_1_q), .b(32'h4), .out(adder_1_out));  // open: cin, cout
  assign bit_extender_1_out = {{6{1'b0}}, shifter_1_out};  // Bit_Extender bit_extender_1
  ROM #(.addrWidth(24), .dataWidth(32)) rom_1 (.addr(shifter_2_out), .data(rom_1_data));  // open: sel
  Multiplexer #(.width(32), .enable("false")) multiplexer_3 (
    .in0(multiplexer_6_out), .in1(adder_1_out), .out(multiplexer_3_out), .sel(control_1_jal));
  Instruction_Splitter instruction_splitter_1 (
    .in_1(rom_1_data), .Function(instruction_splitter_1_function),
    .Constant_Address(instruction_splitter_1_constant_address),
    .Reg_read_rd(instruction_splitter_1_reg_read_rd), .Address(instruction_splitter_1_address),
    .Reg_read_rt(instruction_splitter_1_reg_read_rt), .Reg_read_rs(instruction_splitter_1_reg_read_rs),
    .Opcode(instruction_splitter_1_opcode));
  Multiplexer #(.select(2), .width(5), .enable("false")) multiplexer_4 (
    .in0(instruction_splitter_1_reg_read_rt), .in1(instruction_splitter_1_reg_read_rd), .in2(5'b10001),
    .out(multiplexer_4_out), .sel(undriven));  // open: in3
  assign bit_extender_2_out = {{16{instruction_splitter_1_constant_address[15]}}, instruction_splitter_1_constant_address};  // Bit_Extender bit_extender_2
  Control control_1 (
    .Opcode(instruction_splitter_1_opcode), .RegWrite(control_1_regwrite), .ALUSrc(control_1_alusrc),
    .Branch(control_1_branch), .MemToReg(control_1_memtoreg), .Memwrite(control_1_memwrite),
    .ALUop(control_1_aluop), .Jump(control_1_jump), .JAL(control_1_jal));  // open: RegDst
  reg32 reg32_1 (
    .Read_0(instruction_splitter_1_reg_read_rs), .Read_1(instruction_splitter_1_reg_read_rt),
    .write_addr(multiplexer_4_out), .RegWrite(control_1_regwrite), .Clock(clock_1_out),
    .write_value(multiplexer_3_out), .Value_0(reg32_1_value_0), .Value_1(reg32_1_value_1));  // open: RegClear
  Multiplexer #(.width(32), .enable("false")) multiplexer_5 (
    .in0(reg32_1_value_1), .in1(bit_extender_2_out), .out(multiplexer_5_out), .sel(control_1_alusrc));
  ALU alu_1 (
    .Function(instruction_splitter_1_function), .Input_A(reg32_1_value_0), .Input_B(multiplexer_5_out),
    .S2S1S0(control_1_aluop), .Zero_bit(alu_1_zero_bit), .out_6(alu_1_out_6));
  Shifter #(.width(32)) shifter_3 (.in(bit_extender_2_out), .\dist (5'b00010), .out(shifter_3_out));
  Adder #(.width(32)) adder_2 (.a(shifter_3_out), .b(adder_1_out), .out(adder_2_out));  // open: cin, cout
  and and_1 (and_1_out, control_1_branch, alu_1_zero_bit);
  Shifter #(.width(24), .shift("lr")) shifter_4 (.in(alu_1_out_6[23:0]), .\dist (5'b00010), .out(shifter_4_out));
  RAM #(.addrWidth(24), .dataWidth(32), .bus("separate")) ram_1 (
    .addr(shifter_4_out), .din(reg32_1_value_1), .data(ram_1_data), .str(control_1_memtoreg),
    .clk(clock_1_out));  // open: sel, ld, clr
  Multiplexer #(.width(32), .enable("false")) multiplexer_6 (
    .in0(alu_1_out_6), .in1(ram_1_data), .out(multiplexer_6_out), .sel(control_1_memwrite));

  // Notes on the sheet:
  //   contents of rom_1 (hex, n*v repeats v):
  //   20020005 2003000c 2067fff7 e22025 642824 a42820 10a7000a 64202a 10800001 20050000 e2202a 853820
  //   e23822 ac670044 8c020050 8000011 20020001 ac020054
  //   Memory location 84(01010100) is shifted right by 2 (010101) and then stored in RAM
endmodule

module reg32 (
  input  [4:0] Read_0,
  input  [4:0] Read_1,
  input  [4:0] write_addr,
  input  [31:0] write_value,
  input  Clock,
  input  RegClear,
  input  RegWrite,
  output [31:0] Value_0,
  output [31:0] Value_1
);

  wire and_1_out, and_2_out, and_3_out, and_4_out, and_5_out, and_6_out, and_7_out, and_8_out, and_9_out,
       and_10_out, and_11_out, and_12_out, and_13_out, and_14_out, and_15_out, and_16_out, and_17_out,
       and_18_out, and_19_out, and_20_out, and_21_out, and_22_out, and_23_out, and_24_out, and_25_out,
       and_26_out, and_27_out, and_28_out, and_29_out, and_30_out, and_31_out, decoder_1_out1,
       decoder_1_out2, decoder_1_out3, decoder_1_out4, decoder_1_out5, decoder_1_out6, decoder_1_out7,
       decoder_1_out8, decoder_1_out9, decoder_1_out10, decoder_1_out11, decoder_1_out12, decoder_1_out13,
       decoder_1_out14, decoder_1_out15, decoder_1_out16, decoder_1_out17, decoder_1_out18, decoder_1_out19,
       decoder_1_out20, decoder_1_out21, decoder_1_out22, decoder_1_out23, decoder_1_out24, decoder_1_out25,
       decoder_1_out26, decoder_1_out27, decoder_1_out28, decoder_1_out29, decoder_1_out30, decoder_1_out31;
  wire [31:0] a0_q, a1_q, a2_q, a3_q, at_q, fp_q, gp_q, k0_q, k1_q, ra_q, s0_q, s1_q, s2_q, s3_q, s4_q, s5_q,
       s6_q, s7_q, sp_q, t0_q, t1_q, t2_q, t3_q, t4_q, t5_q, t6_q, t7_q, t8_q, t9_q, v0_q, v1_q;

  Decoder #(.select(5)) decoder_1 (
    .out1(decoder_1_out1), .out2(decoder_1_out2), .out3(decoder_1_out3), .out4(decoder_1_out4),
    .out5(decoder_1_out5), .out6(decoder_1_out6), .out7(decoder_1_out7), .out8(decoder_1_out8),
    .out9(decoder_1_out9), .out10(decoder_1_out10), .out11(decoder_1_out11), .out12(decoder_1_out12),
    .out13(decoder_1_out13), .out14(decoder_1_out14), .out15(decoder_1_out15), .out16(decoder_1_out16),
    .out17(decoder_1_out17), .out18(decoder_1_out18), .out19(decoder_1_out19), .out20(decoder_1_out20),
    .out21(decoder_1_out21), .out22(decoder_1_out22), .out23(decoder_1_out23), .out24(decoder_1_out24),
    .out25(decoder_1_out25), .out26(decoder_1_out26), .out27(decoder_1_out27), .out28(decoder_1_out28),
    .out29(decoder_1_out29), .out30(decoder_1_out30), .out31(decoder_1_out31), .sel(write_addr));  // open: out0, en
  and and_1 (and_1_out, decoder_1_out1, RegWrite);
  and and_2 (and_2_out, RegWrite, decoder_1_out2);
  and and_3 (and_3_out, RegWrite, decoder_1_out3);
  and and_4 (and_4_out, RegWrite, decoder_1_out4);
  and and_5 (and_5_out, RegWrite, decoder_1_out5);
  and and_6 (and_6_out, RegWrite, decoder_1_out6);
  and and_7 (and_7_out, RegWrite, decoder_1_out7);
  and and_8 (and_8_out, RegWrite, decoder_1_out8);
  and and_9 (and_9_out, RegWrite, decoder_1_out9);
  and and_10 (and_10_out, RegWrite, decoder_1_out10);
  and and_11 (and_11_out, RegWrite, decoder_1_out11);
  and and_12 (and_12_out, RegWrite, decoder_1_out12);
  and and_13 (and_13_out, RegWrite, decoder_1_out13);
  and and_14 (and_14_out, RegWrite, decoder_1_out14);
  and and_15 (and_15_out, RegWrite, decoder_1_out15);
  and and_16 (and_16_out, decoder_1_out16, RegWrite);
  and and_17 (and_17_out, decoder_1_out17, RegWrite);
  and and_18 (and_18_out, decoder_1_out18, RegWrite);
  and and_19 (and_19_out, decoder_1_out19, RegWrite);
  and and_20 (and_20_out, decoder_1_out20, RegWrite);
  and and_21 (and_21_out, decoder_1_out21, RegWrite);
  and and_22 (and_22_out, decoder_1_out22, RegWrite);
  and and_23 (and_23_out, decoder_1_out23, RegWrite);
  and and_24 (and_24_out, decoder_1_out24, RegWrite);
  and and_25 (and_25_out, decoder_1_out25, RegWrite);
  and and_26 (and_26_out, decoder_1_out26, RegWrite);
  and and_27 (and_27_out, decoder_1_out27, RegWrite);
  and and_28 (and_28_out, decoder_1_out28, RegWrite);
  and and_29 (and_29_out, decoder_1_out29, RegWrite);
  and and_30 (and_30_out, decoder_1_out30, RegWrite);
  and and_31 (and_31_out, decoder_1_out31, RegWrite);
  Register #(.width(32)) at (.D(write_value), .en(and_1_out), .Q(at_q), .clk(Clock), .clr(RegClear));
  Register #(.width(32)) v0 (.D(write_value), .en(and_2_out), .Q(v0_q), .clk(Clock), .clr(RegClear));
  Register #(.width(32)) v1 (.D(write_value), .en(and_3_out), .Q(v1_q), .clk(Clock), .clr(RegClear));
  Register #(.width(32)) a0 (.D(write_value), .en(and_4_out), .Q(a0_q), .clk(Clock), .clr(RegClear));
  Register #(.width(32)) a1 (.D(write_value), .en(and_5_out), .Q(a1_q), .clk(Clock), .clr(RegClear));
  Register #(.width(32)) a2 (.D(write_value), .en(and_6_out), .Q(a2_q), .clk(Clock), .clr(RegClear));
  Register #(.width(32)) a3 (.D(write_value), .en(and_7_out), .Q(a3_q), .clk(Clock), .clr(RegClear));
  Register #(.width(32)) t0 (.D(write_value), .en(and_8_out), .Q(t0_q), .clk(Clock), .clr(RegClear));
  Register #(.width(32)) t1 (.D(write_value), .en(and_9_out), .Q(t1_q), .clk(Clock), .clr(RegClear));
  Register #(.width(32)) t2 (.D(write_value), .en(and_10_out), .Q(t2_q), .clk(Clock), .clr(RegClear));
  Register #(.width(32)) t3 (.D(write_value), .en(and_11_out), .Q(t3_q), .clk(Clock), .clr(RegClear));
  Register #(.width(32)) t4 (.D(write_value), .en(and_12_out), .Q(t4_q), .clk(Clock), .clr(RegClear));
  Register #(.width(32)) t5 (.D(write_value), .en(and_13_out), .Q(t5_q), .clk(Clock), .clr(RegClear));
  Register #(.width(32)) t6 (.D(write_value), .en(and_14_out), .Q(t6_q), .clk(Clock), .clr(RegClear));
  Register #(.width(32)) t7 (.D(write_value), .en(and_15_out), .Q(t7_q), .clk(Clock), .clr(RegClear));
  Register #(.width(32)) s0 (.D(write_value), .en(and_16_out), .Q(s0_q), .clk(Clock), .clr(RegClear));
  Register #(.width(32)) s1 (.D(write_value), .en(and_17_out), .Q(s1_q), .clk(Clock), .clr(RegClear));
  Register #(.width(32)) s2 (.D(write_value), .en(and_18_out), .Q(s2_q), .clk(Clock), .clr(RegClear));
  Register #(.width(32)) s3 (.D(write_value), .en(and_19_out), .Q(s3_q), .clk(Clock), .clr(RegClear));
  Register #(.width(32)) s4 (.D(write_value), .en(and_20_out), .Q(s4_q), .clk(Clock), .clr(RegClear));
  Register #(.width(32)) s5 (.D(write_value), .en(and_21_out), .Q(s5_q), .clk(Clock), .clr(RegClear));
  Register #(.width(32)) s6 (.D(write_value), .en(and_22_out), .Q(s6_q), .clk(Clock), .clr(RegClear));
  Register #(.width(32)) s7 (.D(write_value), .en(and_23_out), .Q(s7_q), .clk(Clock), .clr(RegClear));
  Register #(.width(32)) t8 (.D(write_value), .en(and_24_out), .Q(t8_q), .clk(Clock), .clr(RegClear));
  Register #(.width(32)) t9 (.D(write_value), .en(and_25_out), .Q(t9_q), .clk(Clock), .clr(RegClear));
  Register #(.width(32)) k0 (.D(write_value), .en(and_26_out), .Q(k0_q), .clk(Clock), .clr(RegClear));
  Register #(.width(32)) k1 (.D(write_value), .en(and_27_out), .Q(k1_q), .clk(Clock), .clr(RegClear));
  Register #(.width(32)) gp (.D(write_value), .en(and_28_out), .Q(gp_q), .clk(Clock), .clr(RegClear));
  Register #(.width(32)) sp (.D(write_value), .en(and_29_out), .Q(sp_q), .clk(Clock), .clr(RegClear));
  Register #(.width(32)) fp (.D(write_value), .en(and_30_out), .Q(fp_q), .clk(Clock), .clr(RegClear));
  Register #(.width(32)) ra (.D(write_value), .en(and_31_out), .Q(ra_q), .clk(Clock), .clr(RegClear));
  Multiplexer #(.select(5), .width(32)) multiplexer_1 (
    .in0({32{1'b0}}), .in1(at_q), .in2(v0_q), .in3(v1_q), .in4(a0_q), .in5(a1_q), .in6(a2_q), .in7(a3_q),
    .in8(t0_q), .in9(t1_q), .in10(t2_q), .in11(t3_q), .in12(t4_q), .in13(t5_q), .in14(t6_q), .in15(t7_q),
    .in16(s0_q), .in17(s1_q), .in18(s2_q), .in19(s3_q), .in20(s4_q), .in21(s5_q), .in22(s6_q), .in23(s7_q),
    .in24(t8_q), .in25(t9_q), .in26(k0_q), .in27(k1_q), .in28(gp_q), .in29(sp_q), .in30(fp_q), .in31(ra_q),
    .out(Value_0), .sel(Read_0));  // open: en
  Multiplexer #(.select(5), .width(32)) multiplexer_2 (
    .in0({32{1'b0}}), .in1(at_q), .in2(v0_q), .in3(v1_q), .in4(a0_q), .in5(a1_q), .in6(a2_q), .in7(a3_q),
    .in8(t0_q), .in9(t1_q), .in10(t2_q), .in11(t3_q), .in12(t4_q), .in13(t5_q), .in14(t6_q), .in15(t7_q),
    .in16(s0_q), .in17(s1_q), .in18(s2_q), .in19(s3_q), .in20(s4_q), .in21(s5_q), .in22(s6_q), .in23(s7_q),
    .in24(t8_q), .in25(t9_q), .in26(k0_q), .in27(k1_q), .in28(gp_q), .in29(sp_q), .in30(fp_q), .in31(ra_q),
    .out(Value_1), .sel(Read_1));  // open: en
endmodule

module Instruction_Splitter (
  input  [31:0] in_1,
  output [5:0] Function,
  output [15:0] Constant_Address,
  output [4:0] Reg_read_rd,
  output [25:0] Address,
  output [4:0] Reg_read_rt,
  output [4:0] Reg_read_rs,
  output [5:0] Opcode
);


  assign Address = in_1[25:0];
  assign Constant_Address = in_1[15:0];
  assign Function = in_1[5:0];
  assign Opcode = in_1[31:26];
  assign Reg_read_rd = in_1[15:11];
  assign Reg_read_rs = in_1[25:21];
  assign Reg_read_rt = in_1[20:16];
endmodule

module ALU (
  input  [5:0] Function,
  input  [31:0] Input_A,
  input  [31:0] Input_B,
  input  [2:0] S2S1S0,
  output Zero_bit,
  output [31:0] out_6
);

  wire comparator_1_lt, comparator_2_lt;
  wire [2:0] alucont_1_p2;
  wire [31:0] adder_1_out, adder_2_out, and_1_out, and_2_out, bit_extender_1_out, bit_extender_2_out,
       multiplexer_2_out, or_1_out, or_2_out, subtractor_1_out, subtractor_2_out;

  // ALUcont alucont_1: pin names not known; wires that end beside it: Function, alucont_1_p2, alucont_1_p2
  Comparator #(.width(32)) comparator_1 (.a(Input_A), .b(Input_B), .lt(comparator_1_lt));  // open: gt, eq
  Adder #(.width(32)) adder_1 (.a(Input_A), .b(Input_B), .out(adder_1_out));  // open: cin, cout
  Subtractor #(.width(32)) subtractor_1 (.a(Input_A), .b(Input_B), .out(subtractor_1_out));  // open: bin, bout
  assign or_1_out = Input_A | Input_B;  // OR_Gate or_1, 32 bits wide
  assign and_1_out = Input_A & Input_B;  // AND_Gate and_1, 32 bits wide
  assign bit_extender_1_out = {{31{1'b0}}, comparator_1_lt};  // Bit_Extender bit_extender_1
  Adder #(.width(32)) adder_2 (.a(Input_A), .b(Input_B), .out(adder_2_out));  // open: cin, cout
  Subtractor #(.width(32)) subtractor_2 (.a(Input_A), .b(Input_B), .out(subtractor_2_out));  // open: bin, bout
  assign or_2_out = Input_A | Input_B;  // OR_Gate or_2, 32 bits wide
  assign and_2_out = Input_A & Input_B;  // AND_Gate and_2, 32 bits wide
  Comparator #(.width(32)) comparator_2 (.a(Input_A), .b(Input_B), .lt(comparator_2_lt));  // open: gt, eq
  assign bit_extender_2_out = {{31{1'b0}}, comparator_2_lt};  // Bit_Extender bit_extender_2
  Multiplexer #(.select(3), .width(32), .enable("false")) multiplexer_1 (
    .in0(multiplexer_2_out), .in1(adder_1_out), .in2(subtractor_1_out), .in3(or_1_out), .in4(and_1_out),
    .in5(bit_extender_1_out), .out(out_6), .sel(S2S1S0));  // open: in6, in7
  Multiplexer #(.select(3), .width(32), .enable("false")) multiplexer_2 (
    .in1(adder_2_out), .in2(subtractor_2_out), .in3(or_2_out), .in4(and_2_out), .in5(bit_extender_2_out),
    .out(multiplexer_2_out), .sel(alucont_1_p2));  // open: in0, in6, in7
  Comparator #(.width(32)) comparator_3 (.a({32{1'b0}}), .b(out_6), .eq(Zero_bit));  // open: gt, lt
endmodule

module Control (
  input  [5:0] Opcode,
  output RegWrite,
  output [1:0] RegDst,
  output ALUSrc,
  output Branch,
  output MemToReg,
  output Memwrite,
  output [2:0] ALUop,
  output Jump,
  output JAL
);

  wire and_1_out, and_2_out, not_1_out, not_2_out, not_3_out, not_4_out, not_5_out, not_6_out, not_7_out,
       not_8_out;

  not not_1 (not_1_out, Opcode[2]);
  and and_1 (and_1_out, not_1_out, not_2_out);
  not not_2 (not_2_out, Opcode[1]);
  not not_3 (not_3_out, Opcode[3]);
  and and_2 (and_2_out, not_3_out, Opcode[0]);
  not not_4 (not_4_out, Opcode[5]);
  and and_3 (RegDst[1], not_4_out, Opcode[1]);
  not not_5 (not_5_out, Opcode[3]);
  and and_4 (RegDst[0], not_5_out, not_6_out);
  not not_6 (not_6_out, Opcode[1]);
  or or_1 (ALUSrc, Opcode[1], Opcode[3]);
  and and_5 (Memwrite, Opcode[5], Opcode[3]);
  or or_2 (ALUop[0], Opcode[1], Opcode[3]);
  not not_7 (not_7_out, Opcode[5]);
  and and_6 (Jump, not_7_out, Opcode[1]);
  not not_8 (not_8_out, Opcode[5]);
  and and_7 (JAL, not_8_out, Opcode[0]);
  or or_3 (RegWrite, and_1_out, and_2_out);

  assign ALUop[2:1] = {1'b0, Opcode[2]};
  assign Branch = Opcode[2];
  assign MemToReg = Opcode[1];
endmodule

module ALUcont (
  input  [31:0] Input_A,
  input  [31:0] Input_B,
  input  [2:0] in_3,
  output Zero_Bit,
  output [31:0] out_5
);

  wire [31:0] adder_1_out, and_1_out, bit_extender_1_out, multiplexer_1_out, not_1_out, or_1_out;

  assign not_1_out = ~Input_B;  // NOT_Gate not_1, 32 bits wide
  Multiplexer #(.width(32), .enable("false")) multiplexer_1 (
    .in0(Input_B), .in1(not_1_out), .out(multiplexer_1_out), .sel(in_3[2]));
  Adder #(.width(32)) adder_1 (.a(Input_A), .b(multiplexer_1_out), .out(adder_1_out), .cin(in_3[2]));  // open: cout
  assign or_1_out = multiplexer_1_out | Input_A;  // OR_Gate or_1, 32 bits wide
  assign and_1_out = multiplexer_1_out & Input_A;  // AND_Gate and_1, 32 bits wide
  assign bit_extender_1_out = {{31{1'b0}}, adder_1_out[31]};  // Bit_Extender bit_extender_1
  Multiplexer #(.select(2), .width(32), .enable("false")) multiplexer_2 (
    .in0(and_1_out), .in1(or_1_out), .in2(adder_1_out), .in3(bit_extender_1_out), .out(out_5), .sel(in_3[1:0]));
  Comparator #(.width(32)) comparator_1 (.a({32{1'b0}}), .b(out_5), .eq(Zero_Bit));  // open: gt, lt
endmodule

module General (
  input  in_1,
  input  in_2,
  input  in_3,
  input  in_4,
  input  in_5,
  input  [6:0] in_6,
  input  in_7
);

  wire clock_1_out, clock_2_out;
  wire [7:0] random_1_out, random_2_out;

  Random random_1 (.clk(clock_1_out), .out(random_1_out));  // open: next, clr
  Clock clock_1 (.out(clock_1_out));
  Random random_2 (.clk(clock_1_out), .out(random_2_out));  // open: next, clr
  RAM #(.bus("separate")) ram_1 (
    .addr(random_1_out), .din(random_2_out), .str(in_5), .clk(clock_1_out));  // open: data, sel, ld, clr
  _7_Segment_Display u_7_segment_display_1 (.g(in_4), .f(in_1), .a(in_2), .b(in_3), .dp(in_3));  // open: e, d, c
  Clock clock_2 (.out(clock_2_out));
  TTY tty_1 (.data(in_6), .clk(clock_2_out), .we(in_7));  // open: clr
  _7_Segment_Display u_7_segment_display_2 ();  // open: g, f, a, b, e, d, c, dp
endmodule

module Datapath_ex (
  input  in_1,
  input  [2:0] in_2,
  input  in_3,
  input  in_4,
  input  in_5,
  input  Clear_PC
);

  wire alu_1_zero_bit, clock_1_out, undriven;
  wire [4:0] instruction_splitter_1_reg_read_rd, instruction_splitter_1_reg_read_rs,
       instruction_splitter_1_reg_read_rt;
  wire [5:0] instruction_splitter_1_function, instruction_splitter_1_opcode;
  wire [15:0] instruction_splitter_1_constant_address;
  wire [23:0] shifter_1_out, shifter_2_out;
  wire [25:0] instruction_splitter_1_address;
  wire [31:0] adder_1_out, alu_1_out_6, bit_extender_1_out, multiplexer_1_out, multiplexer_2_out,
       multiplexer_3_out, ram_1_data, reg32_1_value_0, reg32_1_value_1, register_1_q, rom_1_data;

  Clock clock_1 (.out(clock_1_out));
  Register #(.width(32)) register_1 (.D(adder_1_out), .Q(register_1_q), .clk(clock_1_out), .clr(Clear_PC));  // open: en
  Shifter #(.width(24), .shift("lr")) shifter_1 (.in(register_1_q[23:0]), .\dist (5'b00010), .out(shifter_1_out));
  Adder #(.width(32)) adder_1 (.a(register_1_q), .b(32'h4), .out(adder_1_out));  // open: cin, cout
  ROM #(.addrWidth(24), .dataWidth(32)) rom_1 (.addr(shifter_1_out), .data(rom_1_data));  // open: sel
  Multiplexer #(.width(32), .enable("false")) multiplexer_1 (
    .in0(multiplexer_3_out), .in1(adder_1_out), .out(multiplexer_1_out), .sel(in_3));
  Instruction_Splitter instruction_splitter_1 (
    .in_1(rom_1_data), .Function(instruction_splitter_1_function),
    .Constant_Address(instruction_splitter_1_constant_address),
    .Reg_read_rd(instruction_splitter_1_reg_read_rd), .Address(instruction_splitter_1_address),
    .Reg_read_rt(instruction_splitter_1_reg_read_rt), .Reg_read_rs(instruction_splitter_1_reg_read_rs),
    .Opcode(instruction_splitter_1_opcode));
  assign bit_extender_1_out = {{16{instruction_splitter_1_constant_address[15]}}, instruction_splitter_1_constant_address};  // Bit_Extender bit_extender_1
  reg32 reg32_1 (
    .Read_0(instruction_splitter_1_reg_read_rs), .write_addr(instruction_splitter_1_reg_read_rt),
    .RegWrite(in_1), .Clock(clock_1_out), .write_value(multiplexer_1_out), .Value_0(reg32_1_value_0),
    .Value_1(reg32_1_value_1));  // open: Read_1, RegClear
  Multiplexer #(.width(32), .enable("false")) multiplexer_2 (
    .in0(reg32_1_value_1), .in1(bit_extender_1_out), .out(multiplexer_2_out), .sel(in_5));
  ALU alu_1 (
    .Function(instruction_splitter_1_function), .Input_A(reg32_1_value_0), .Input_B(multiplexer_2_out),
    .S2S1S0(in_2), .Zero_bit(alu_1_zero_bit), .out_6(alu_1_out_6));
  Shifter #(.width(24), .shift("lr")) shifter_2 (.in(alu_1_out_6[23:0]), .\dist (5'b00010), .out(shifter_2_out));
  RAM #(.addrWidth(24), .dataWidth(32), .bus("separate")) ram_1 (
    .addr(shifter_2_out), .din(reg32_1_value_1), .data(ram_1_data), .str(undriven), .clk(clock_1_out));  // open: sel, ld, clr
  Multiplexer #(.width(32), .enable("false")) multiplexer_3 (
    .in0(alu_1_out_6), .in1(ram_1_data), .out(multiplexer_3_out), .sel(in_4));

  // Notes on the sheet:
  //   load word
  //   contents of rom_1 (hex, n*v repeats v):
  //   8c020004 c0100014 2067fff7 e22025 642824 a42820 10a7000a 64202a 10800001 20050000 e2202a 853820
  //   e23822 ac670044 8c020050 8000011 20020001 ac020054
endmodule

module datapath_sw (
  input  in_1,
  input  [2:0] in_2,
  input  in_3,
  input  in_4,
  input  in_5,
  input  Clear_PC
);

  wire alu_1_zero_bit, clock_1_out, undriven;
  wire [4:0] instruction_splitter_1_reg_read_rd, instruction_splitter_1_reg_read_rs,
       instruction_splitter_1_reg_read_rt;
  wire [5:0] instruction_splitter_1_function, instruction_splitter_1_opcode;
  wire [15:0] instruction_splitter_1_constant_address;
  wire [23:0] shifter_1_out, shifter_2_out;
  wire [25:0] instruction_splitter_1_address;
  wire [31:0] adder_1_out, alu_1_out_6, bit_extender_1_out, multiplexer_1_out, multiplexer_2_out,
       multiplexer_3_out, ram_1_data, reg32_1_value_0, reg32_1_value_1, register_1_q, rom_1_data;

  Clock clock_1 (.out(clock_1_out));
  Register #(.width(32)) register_1 (.D(adder_1_out), .Q(register_1_q), .clk(clock_1_out), .clr(Clear_PC));  // open: en
  Shifter #(.width(24), .shift("lr")) shifter_1 (.in(register_1_q[23:0]), .\dist (5'b00010), .out(shifter_1_out));
  Adder #(.width(32)) adder_1 (.a(register_1_q), .b(32'h4), .out(adder_1_out));  // open: cin, cout
  ROM #(.addrWidth(24), .dataWidth(32)) rom_1 (.addr(shifter_1_out), .data(rom_1_data));  // open: sel
  Multiplexer #(.width(32), .enable("false")) multiplexer_1 (
    .in0(multiplexer_3_out), .in1(adder_1_out), .out(multiplexer_1_out), .sel(in_3));
  Instruction_Splitter instruction_splitter_1 (
    .in_1(rom_1_data), .Function(instruction_splitter_1_function),
    .Constant_Address(instruction_splitter_1_constant_address),
    .Reg_read_rd(instruction_splitter_1_reg_read_rd), .Address(instruction_splitter_1_address),
    .Reg_read_rt(instruction_splitter_1_reg_read_rt), .Reg_read_rs(instruction_splitter_1_reg_read_rs),
    .Opcode(instruction_splitter_1_opcode));
  assign bit_extender_1_out = {{16{instruction_splitter_1_constant_address[15]}}, instruction_splitter_1_constant_address};  // Bit_Extender bit_extender_1
  reg32 reg32_1 (
    .Read_0(instruction_splitter_1_reg_read_rs), .write_addr(instruction_splitter_1_reg_read_rt),
    .RegWrite(in_1), .Clock(clock_1_out), .write_value(multiplexer_1_out), .Value_0(reg32_1_value_0),
    .Value_1(reg32_1_value_1));  // open: Read_1, RegClear
  Multiplexer #(.width(32), .enable("false")) multiplexer_2 (
    .in0(reg32_1_value_1), .in1(bit_extender_1_out), .out(multiplexer_2_out), .sel(in_5));
  ALU alu_1 (
    .Function(instruction_splitter_1_function), .Input_A(reg32_1_value_0), .Input_B(multiplexer_2_out),
    .S2S1S0(in_2), .Zero_bit(alu_1_zero_bit), .out_6(alu_1_out_6));
  Shifter #(.width(24), .shift("lr")) shifter_2 (.in(alu_1_out_6[23:0]), .\dist (5'b00010), .out(shifter_2_out));
  RAM #(.addrWidth(24), .dataWidth(32), .bus("separate")) ram_1 (
    .addr(shifter_2_out), .din(reg32_1_value_1), .data(ram_1_data), .str(undriven), .clk(clock_1_out));  // open: sel, ld, clr
  Multiplexer #(.width(32), .enable("false")) multiplexer_3 (
    .in0(alu_1_out_6), .in1(ram_1_data), .out(multiplexer_3_out), .sel(in_4));

  // Notes on the sheet:
  //   contents of rom_1 (hex, n*v repeats v):
  //   8c020004 c0100014 2067fff7 e22025 642824 a42820 10a7000a 64202a 10800001 20050000 e2202a 853820
  //   e23822 ac670044 8c020050 8000011 20020001 ac020054
endmodule

module ALU_2101CS09 (
  input  [31:0] in_1,
  input  [2:0] in_2,
  input  [31:0] in_3,
  output out_4,
  output [31:0] out_5
);

  wire [31:0] adder_1_out, and_1_out, bit_extender_1_out, multiplexer_2_out, not_1_out, or_1_out;

  Multiplexer #(.select(2), .width(32), .enable("false")) multiplexer_1 (
    .in0(and_1_out), .in1(or_1_out), .in2(adder_1_out), .in3(bit_extender_1_out), .out(out_5), .sel(in_2[2:1]));
  assign not_1_out = ~in_1;  // NOT_Gate not_1, 32 bits wide
  Multiplexer #(.width(32), .enable("false")) multiplexer_2 (
    .in0(in_1), .in1(not_1_out), .out(multiplexer_2_out), .sel(in_2[0]));
  Adder #(.width(32)) adder_1 (.a(in_3), .b(multiplexer_2_out), .out(adder_1_out), .cin(in_2[0]), .cout(out_4));
  assign or_1_out = in_3 | multiplexer_2_out;  // OR_Gate or_1, 32 bits wide
  assign and_1_out = in_3 & multiplexer_2_out;  // AND_Gate and_1, 32 bits wide
  assign bit_extender_1_out = {{31{1'b0}}, adder_1_out[31]};  // Bit_Extender bit_extender_1

  // Notes on the sheet:
  //   ARITHMETIC LOGIC UNIT (ALU)
  //   MULTIPLEXER
  //   MULTIPLEXER
  //   ADDER
  //   BIT EXTENDER
endmodule

module Datapath_LW (
  input  [2:0] in_1,
  input  in_2,
  input  in_3,
  input  in_4
);

  wire clock_1_out;
  wire [4:0] instruction_splitter_1_reg_read_rs, instruction_splitter_1_reg_read_rt;
  wire [15:0] instruction_splitter_1_constant_address;
  wire [23:0] shifter_1_out, shifter_2_out;
  wire [31:0] adder_1_out, alucont_1_out_5, bit_extender_1_out, ram_1_data, reg32_1_value_0, register_1_q,
       rom_1_data;

  Clock clock_1 (.out(clock_1_out));
  Register #(.width(32)) register_1 (.D(adder_1_out), .Q(register_1_q), .clk(clock_1_out), .clr(in_4));  // open: en
  Shifter #(.width(24), .shift("lr")) shifter_1 (.in(register_1_q[23:0]), .\dist (5'b00010), .out(shifter_1_out));
  Adder #(.width(32)) adder_1 (.a(register_1_q), .b(32'h4), .out(adder_1_out));  // open: cin, cout
  ROM #(.addrWidth(24), .dataWidth(32)) rom_1 (.addr(shifter_1_out), .data(rom_1_data));  // open: sel
  Instruction_Splitter instruction_splitter_1 (
    .in_1(rom_1_data), .Constant_Address(instruction_splitter_1_constant_address),
    .Reg_read_rt(instruction_splitter_1_reg_read_rt), .Reg_read_rs(instruction_splitter_1_reg_read_rs));  // open: Function, Reg_read_rd, Address, Opcode
  assign bit_extender_1_out = {{16{instruction_splitter_1_constant_address[15]}}, instruction_splitter_1_constant_address};  // Bit_Extender bit_extender_1
  reg32 reg32_1 (
    .Read_0(instruction_splitter_1_reg_read_rs), .write_addr(instruction_splitter_1_reg_read_rt),
    .RegWrite(in_2), .RegClear(in_3), .Clock(clock_1_out), .write_value(ram_1_data), .Value_0(reg32_1_value_0));  // open: Read_1, Value_1
  ALUcont alucont_1 (
    .Input_A(reg32_1_value_0), .Input_B(bit_extender_1_out), .in_3(in_1), .out_5(alucont_1_out_5));  // open: Zero_Bit
  Shifter #(.width(24), .shift("lr")) shifter_2 (.in(alucont_1_out_5[23:0]), .\dist (5'b00010), .out(shifter_2_out));
  RAM #(.addrWidth(24), .dataWidth(32), .bus("separate")) ram_1 (
    .addr(shifter_2_out), .data(ram_1_data), .clk(clock_1_out));  // open: din, str, sel, ld, clr

  // Notes on the sheet:
  //   contents of rom_1 (hex, n*v repeats v):
  //   ac670044 ac670044 2067fff7 e22025 642824 a42820 10a7000a 64202a 10800001 20050000 e2202a 853820
  //   e23822 ac670044 8c020050 8000011 20020001 ac020054
endmodule

module Datapath_SW (
  input  [2:0] in_1,
  input  in_2,
  input  in_3,
  input  [5:0] in_4
);

  wire clock_1_out, control_1_regwrite;
  wire [4:0] instruction_splitter_1_reg_read_rs, instruction_splitter_1_reg_read_rt;
  wire [15:0] instruction_splitter_1_constant_address;
  wire [23:0] shifter_1_out, shifter_2_out;
  wire [31:0] adder_1_out, alucont_1_out_5, bit_extender_1_out, reg32_1_value_0, reg32_1_value_1,
       register_1_q, rom_1_data;

  Clock clock_1 (.out(clock_1_out));
  Register #(.width(32)) register_1 (.D(adder_1_out), .Q(register_1_q), .clk(clock_1_out), .clr(in_3));  // open: en
  Shifter #(.width(24), .shift("lr")) shifter_1 (.in(register_1_q[23:0]), .\dist (5'b00010), .out(shifter_1_out));
  Adder #(.width(32)) adder_1 (.a(register_1_q), .b(32'h4), .out(adder_1_out));  // open: cin, cout
  ROM #(.addrWidth(24), .dataWidth(32)) rom_1 (.addr(shifter_1_out), .data(rom_1_data));  // open: sel
  Instruction_Splitter instruction_splitter_1 (
    .in_1(rom_1_data), .Constant_Address(instruction_splitter_1_constant_address),
    .Reg_read_rt(instruction_splitter_1_reg_read_rt), .Reg_read_rs(instruction_splitter_1_reg_read_rs));  // open: Function, Reg_read_rd, Address, Opcode
  Control control_1 (
    .Opcode(in_4), .RegWrite(control_1_regwrite));  // open: RegDst, ALUSrc, Branch, MemToReg, Memwrite, ALUop, Jump, JAL
  assign bit_extender_1_out = {{16{instruction_splitter_1_constant_address[15]}}, instruction_splitter_1_constant_address};  // Bit_Extender bit_extender_1
  reg32 reg32_1 (
    .Read_0(instruction_splitter_1_reg_read_rs), .Read_1(instruction_splitter_1_reg_read_rt),
    .RegClear(control_1_regwrite), .Clock(clock_1_out), .Value_0(reg32_1_value_0), .Value_1(reg32_1_value_1));  // open: write_addr, RegWrite, write_value
  ALUcont alucont_1 (
    .Input_A(reg32_1_value_0), .Input_B(bit_extender_1_out), .in_3(in_1), .out_5(alucont_1_out_5));  // open: Zero_Bit
  Shifter #(.width(24), .shift("lr")) shifter_2 (.in(alucont_1_out_5[23:0]), .\dist (5'b00010), .out(shifter_2_out));
  RAM #(.addrWidth(24), .dataWidth(32), .bus("separate")) ram_1 (
    .addr(shifter_2_out), .din(reg32_1_value_1), .str(in_2), .clk(clock_1_out));  // open: data, sel, ld, clr

  // Notes on the sheet:
  //   contents of rom_1 (hex, n*v repeats v):
  //   ac670044 ac670044 2067fff7 e22025 642824 a42820 10a7000a 64202a 10800001 20050000 e2202a 853820
  //   e23822 ac670044 8c020050 8000011 20020001 ac020054
endmodule

module Datapath_Branch_if_equal (
  input  in_1,
  input  [2:0] in_2,
  input  in_3
);

  wire alucont_1_zero_bit, and_1_out, clock_1_out;
  wire [4:0] instruction_splitter_1_reg_read_rs, instruction_splitter_1_reg_read_rt;
  wire [15:0] instruction_splitter_1_constant_address;
  wire [23:0] shifter_1_out;
  wire [31:0] adder_1_out, adder_2_out, bit_extender_1_out, multiplexer_1_out, reg32_1_value_0,
       reg32_1_value_1, register_1_q, rom_1_data, shifter_2_out;

  Multiplexer #(.width(32), .enable("false")) multiplexer_1 (
    .in0(adder_1_out), .in1(adder_2_out), .out(multiplexer_1_out), .sel(and_1_out));
  Clock clock_1 (.out(clock_1_out));
  Register #(.width(32)) register_1 (
    .D(multiplexer_1_out), .Q(register_1_q), .clk(clock_1_out), .clr(in_3));  // open: en
  Shifter #(.width(24), .shift("lr")) shifter_1 (.in(register_1_q[23:0]), .\dist (5'b00010), .out(shifter_1_out));
  Adder #(.width(32)) adder_1 (.a(register_1_q), .b(32'h4), .out(adder_1_out));  // open: cin, cout
  ROM #(.addrWidth(24), .dataWidth(32)) rom_1 (.addr(shifter_1_out), .data(rom_1_data));  // open: sel
  Instruction_Splitter instruction_splitter_1 (
    .in_1(rom_1_data), .Constant_Address(instruction_splitter_1_constant_address),
    .Reg_read_rt(instruction_splitter_1_reg_read_rt), .Reg_read_rs(instruction_splitter_1_reg_read_rs));  // open: Function, Reg_read_rd, Address, Opcode
  assign bit_extender_1_out = {{16{instruction_splitter_1_constant_address[15]}}, instruction_splitter_1_constant_address};  // Bit_Extender bit_extender_1
  reg32 reg32_1 (
    .Read_0(instruction_splitter_1_reg_read_rs), .Read_1(instruction_splitter_1_reg_read_rt),
    .Value_0(reg32_1_value_0), .Value_1(reg32_1_value_1));  // open: write_addr, RegWrite, RegClear, Clock, write_value
  ALUcont alucont_1 (
    .Input_A(reg32_1_value_0), .Input_B(reg32_1_value_1), .in_3(in_2), .Zero_Bit(alucont_1_zero_bit));  // open: out_5
  Shifter #(.width(32)) shifter_2 (.in(bit_extender_1_out), .\dist (5'b00010), .out(shifter_2_out));
  and and_1 (and_1_out, in_1, alucont_1_zero_bit);
  Adder #(.width(32)) adder_2 (.a(shifter_2_out), .b(adder_1_out), .out(adder_2_out));  // open: cin, cout

  // Notes on the sheet:
  //   contents of rom_1 (hex, n*v repeats v):
  //   10071000 c0100014 2067fff7 e22025 642824 a42820 10a7000a 64202a 10800001 20050000 e2202a 853820
  //   e23822 ac670044 8c020050 8000011 20020001 ac020054
endmodule
