// Logisim project 2101CS09_lab6.circ as structural Verilog: 14 circuits, main circuit reg32
module reg32 (
  input  [4:0] A1,
  input  [4:0] A2,
  input  [4:0] A3,
  input  [31:0] WD3,
  input  Clock,
  input  RegClear,
  input  RegWrite,
  output [31:0] RD1,
  output [31:0] RD2
);

  wire and_1_out, and_2_out, and_3_out, and_4_out, and_5_out, and_6_out, and_7_out, and_8_out, and_9_out,
       and_10_out, and_11_out, and_12_out, and_13_out, and_14_out, and_15_out, and_16_out, and_17_out,
       and_18_out, and_19_out, and_20_out, and_21_out, and_22_out, and_23_out, and_24_out, and_25_out,
       and_26_out, and_27_out, and_28_out, and_29_out, and_30_out, and_31_out, decoder_1_out1,
       decoder_1_out2, decoder_1_out3, decoder_1_out4, decoder_1_out5, decoder_1_out6, decoder_1_out7,
       decoder_1_out8, decoder_1_out9, decoder_1_out10, decoder_1_out11, decoder_1_out12, decoder_1_out13,
       decoder_1_out14, decoder_1_out15, decoder_1_out16, decoder_1_out17, decoder_1_out18, decoder_1_out19,
       decoder_1_out20, decoder_1_out21, decoder_1_out22, decoder_1_out23, decoder_1_out24, decoder_1_out25,
       decoder_1_out26, decoder_1_out27, decoder_1_out28, decoder_1_out29, decoder_1_out30, decoder_1_out31;
  wire [31:0] a0_q, a1_q, a2_q, a3_q, at_q, fp_q, gp_q, k0_q, k1_q, ra_q, s0_q, s1_q, s2_q, s3_q, s4_q, s5_q,
       s6_q, s7_q, sp_q, t0_q, t1_q, t2_q, t3_q, t4_q, t5_q, t6_q, t7_q, t8_q, t9_q, v0_q, v1_q;

  Decoder #(.select(5)) decoder_1 (
    .out1(decoder_1_out1), .out2(decoder_1_out2), .out3(decoder_1_out3), .out4(decoder_1_out4),
    .out5(decoder_1_out5), .out6(decoder_1_out6), .out7(decoder_1_out7), .out8(decoder_1_out8),
    .out9(decoder_1_out9), .out10(decoder_1_out10), .out11(decoder_1_out11), .out12(decoder_1_out12),
    .out13(decoder_1_out13), .out14(decoder_1_out14), .out15(decoder_1_out15), .out16(decoder_1_out16),
    .out17(decoder_1_out17), .out18(decoder_1_out18), .out19(decoder_1_out19), .out20(decoder_1_out20),
    .out21(decoder_1_out21), .out22(decoder_1_out22), .out23(decoder_1_out23), .out24(decoder_1_out24),
    .out25(decoder_1_out25), .out26(decoder_1_out26), .out27(decoder_1_out27), .out28(decoder_1_out28),
    .out29(decoder_1_out29), .out30(decoder_1_out30), .out31(decoder_1_out31), .sel(A3));  // open: out0, en
  and and_1 (and_1_out, decoder_1_out1, RegWrite);
  and and_2 (and_2_out, RegWrite, decoder_1_out2);
  and and_3 (and_3_out, RegWrite, decoder_1_out3);
  and and_4 (and_4_out, RegWrite, decoder_1_out4);
  and and_5 (and_5_out, RegWrite, decoder_1_out5);
  and and_6 (and_6_out, RegWrite, decoder_1_out6);
  and and_7 (and_7_out, RegWrite, decoder_1_out7);
  and and_8 (and_8_out, RegWrite, decoder_1_out8);
  and and_9 (and_9_out, RegWrite, decoder_1_out9);
  and and_10 (and_10_out, RegWrite, decoder_1_out10);
  and and_11 (and_11_out, RegWrite, decoder_1_out11);
  and and_12 (and_12_out, RegWrite, decoder_1_out12);
  and and_13 (and_13_out, RegWrite, decoder_1_out13);
  and and_14 (and_14_out, RegWrite, decoder_1_out14);
  and and_15 (and_15_out, RegWrite, decoder_1_out15);
  and and_16 (and_16_out, decoder_1_out16, RegWrite);
  and and_17 (and_17_out, decoder_1_out17, RegWrite);
  and and_18 (and_18_out, decoder_1_out18, RegWrite);
  and and_19 (and_19_out, decoder_1_out19, RegWrite);
  and and_20 (and_20_out, decoder_1_out20, RegWrite);
  and and_21 (and_21_out, decoder_1_out21, RegWrite);
  and and_22 (and_22_out, decoder_1_out22, RegWrite);
  and and_23 (and_23_out, decoder_1_out23, RegWrite);
  and and_24 (and_24_out, decoder_1_out24, RegWrite);
  and and_25 (and_25_out, decoder_1_out25, RegWrite);
  and and_26 (and_26_out, decoder_1_out26, RegWrite);
  and and_27 (and_27_out, decoder_1_out27, RegWrite);
  and and_28 (and_28_out, decoder_1_out28, RegWrite);
  and and_29 (and_29_out, decoder_1_out29, RegWrite);
  and and_30 (and_30_out, decoder_1_out30, RegWrite);
  and and_31 (and_31_out, decoder_1_out31, RegWrite);
  Register #(.width(32)) at (.D(WD3), .en(and_1_out), .Q(at_q), .clk(Clock), .clr(RegClear));
  Register #(.width(32)) v0 (.D(WD3), .en(and_2_out), .Q(v0_q), .clk(Clock), .clr(RegClear));
  Register #(.width(32)) v1 (.D(WD3), .en(and_3_out), .Q(v1_q), .clk(Clock), .clr(RegClear));
  Register #(.width(32)) a0 (.D(WD3), .en(and_4_out), .Q(a0_q), .clk(Clock), .clr(RegClear));
  Register #(.width(32)) u_a1 (.D(WD3), .en(and_5_out), .Q(a1_q), .clk(Clock), .clr(RegClear));
  Register #(.width(32)) u_a2 (.D(WD3), .en(and_6_out), .Q(a2_q), .clk(Clock), .clr(RegClear));
  Register #(.width(32)) u_a3 (.D(WD3), .en(and_7_out), .Q(a3_q), .clk(Clock), .clr(RegClear));
  Register #(.width(32)) t0 (.D(WD3), .en(and_8_out), .Q(t0_q), .clk(Clock), .clr(RegClear));
  Register #(.width(32)) t1 (.D(WD3), .en(and_9_out), .Q(t1_q), .clk(Clock), .clr(RegClear));
  Register #(.width(32)) t2 (.D(WD3), .en(and_10_out), .Q(t2_q), .clk(Clock), .clr(RegClear));
  Register #(.width(32)) t3 (.D(WD3), .en(and_11_out), .Q(t3_q), .clk(Clock), .clr(RegClear));
  Register #(.width(32)) t4 (.D(WD3), .en(and_12_out), .Q(t4_q), .clk(Clock), .clr(RegClear));
  Register #(.width(32)) t5 (.D(WD3), .en(and_13_out), .Q(t5_q), .clk(Clock), .clr(RegClear));
  Register #(.width(32)) t6 (.D(WD3), .en(and_14_out), .Q(t6_q), .clk(Clock), .clr(RegClear));
  Register #(.width(32)) t7 (.D(WD3), .en(and_15_out), .Q(t7_q), .clk(Clock), .clr(RegClear));
  Register #(.width(32)) s0 (.D(WD3), .en(and_16_out), .Q(s0_q), .clk(Clock), .clr(RegClear));
  Register #(.width(32)) s1 (.D(WD3), .en(and_17_out), .Q(s1_q), .clk(Clock), .clr(RegClear));
  Register #(.width(32)) s2 (.D(WD3), .en(and_18_out), .Q(s2_q), .clk(Clock), .clr(RegClear));
  Register #(.width(32)) s3 (.D(WD3), .en(and_19_out), .Q(s3_q), .clk(Clock), .clr(RegClear));
  Register #(.width(32)) s4 (.D(WD3), .en(and_20_out), .Q(s4_q), .clk(Clock), .clr(RegClear));
  Register #(.width(32)) s5 (.D(WD3), .en(and_21_out), .Q(s5_q), .clk(Clock), .clr(RegClear));
  Register #(.width(32)) s6 (.D(WD3), .en(and_22_out), .Q(s6_q), .clk(Clock), .clr(RegClear));
  Register #(.width(32)) s7 (.D(WD3), .en(and_23_out), .Q(s7_q), .clk(Clock), .clr(RegClear));
  Register #(.width(32)) t8 (.D(WD3), .en(and_24_out), .Q(t8_q), .clk(Clock), .clr(RegClear));
  Register #(.width(32)) t9 (.D(WD3), .en(and_25_out), .Q(t9_q), .clk(Clock), .clr(RegClear));
  Register #(.width(32)) k0 (.D(WD3), .en(and_26_out), .Q(k0_q), .clk(Clock), .clr(RegClear));
  Register #(.width(32)) k1 (.D(WD3), .en(and_27_out), .Q(k1_q), .clk(Clock), .clr(RegClear));
  Register #(.width(32)) gp (.D(WD3), .en(and_28_out), .Q(gp_q), .clk(Clock), .clr(RegClear));
  Register #(.width(32)) sp (.D(WD3), .en(and_29_out), .Q(sp_q), .clk(Clock), .clr(RegClear));
  Register #(.width(32)) fp (.D(WD3), .en(and_30_out), .Q(fp_q), .clk(Clock), .clr(RegClear));
  Register #(.width(32)) ra (.D(WD3), .en(and_31_out), .Q(ra_q), .clk(Clock), .clr(RegClear));
  Multiplexer #(.select(5), .width(32)) multiplexer_1 (
    .in0({32{1'b0}}), .in1(at_q), .in2(v0_q), .in3(v1_q), .in4(a0_q), .in5(a1_q), .in6(a2_q), .in7(a3_q),
    .in8(t0_q), .in9(t1_q), .in10(t2_q), .in11(t3_q), .in12(t4_q), .in13(t5_q), .in14(t6_q), .in15(t7_q),
    .in16(s0_q), .in17(s1_q), .in18(s2_q), .in19(s3_q), .in20(s4_q), .in21(s5_q), .in22(s6_q), .in23(s7_q),
    .in24(t8_q), .in25(t9_q), .in26(k0_q), .in27(k1_q), .in28(gp_q), .in29(sp_q), .in30(fp_q), .in31(ra_q),
    .out(RD1), .sel(A1));  // open: en
  Multiplexer #(.select(5), .width(32)) multiplexer_2 (
    .in0({32{1'b0}}), .in1(at_q), .in2(v0_q), .in3(v1_q), .in4(a0_q), .in5(a1_q), .in6(a2_q), .in7(a3_q),
    .in8(t0_q), .in9(t1_q), .in10(t2_q), .in11(t3_q), .in12(t4_q), .in13(t5_q), .in14(t6_q), .in15(t7_q),
    .in16(s0_q), .in17(s1_q), .in18(s2_q), .in19(s3_q), .in20(s4_q), .in21(s5_q), .in22(s6_q), .in23(s7_q),
    .in24(t8_q), .in25(t9_q), .in26(k0_q), .in27(k1_q), .in28(gp_q), .in29(sp_q), .in30(fp_q), .in31(ra_q),
    .out(RD2), .sel(A2));  // open: en
endmodule

// ins aplitterr
module Instruction_Splitter (
  input  [31:0] in_1,
  output [5:0] _5_0_func,
  output [15:0] _15_0_imm,
  output [4:0] _15_11_rd,
  output [25:0] _25_0_jump,
  output [4:0] _20_16_rt,
  output [4:0] _25_21_rs,
  output [5:0] _31_26_OpCode
);


  assign _5_0_func = in_1[5:0];
  assign _15_0_imm = in_1[15:0];
  assign _15_11_rd = in_1[15:11];
  assign _20_16_rt = in_1[20:16];
  assign _25_0_jump = in_1[25:0];
  assign _25_21_rs = in_1[25:21];
  assign _31_26_OpCode = in_1[31:26];
endmodule

module ALU (
  input  [5:0] Function,
  input  [31:0] Input_A,
  input  [31:0] Input_B,
  input  [2:0] S2S1S0,
  output Zero_bit,
  output [31:0] out_6
);

  wire comparator_1_lt, comparator_2_lt;
  wire [2:0] alucont_1_out_2;
  wire [31:0] adder_1_out, adder_2_out, and_1_out, and_2_out, bit_extender_1_out, bit_extender_2_out,
       multiplexer_2_out, or_1_out, or_2_out, subtractor_1_out, subtractor_2_out;

  ALUcont alucont_1 (.in_1(Function), .out_2(alucont_1_out_2));
  Comparator #(.width(32)) comparator_1 (.a(Input_A), .b(Input_B), .lt(comparator_1_lt));  // open: gt, eq
  Adder #(.width(32)) adder_1 (.a(Input_A), .b(Input_B), .out(adder_1_out));  // open: cin, cout
  Subtractor #(.width(32)) subtractor_1 (.a(Input_A), .b(Input_B), .out(subtractor_1_out));  // open: bin, bout
  assign or_1_out = Input_A | Input_B;  // OR_Gate or_1, 32 bits wide
  assign and_1_out = Input_A & Input_B;  // AND_Gate and_1, 32 bits wide
  assign bit_extender_1_out = {{31{1'b0}}, comparator_1_lt};  // Bit_Extender bit_extender_1
  Adder #(.width(32)) adder_2 (.a(Input_A), .b(Input_B), .out(adder_2_out));  // open: cin, cout
  Subtractor #(.width(32)) subtractor_2 (.a(Input_A), .b(Input_B), .out(subtractor_2_out));  // open: bin, bout
  assign or_2_out = Input_A | Input_B;  // OR_Gate or_2, 32 bits wide
  assign and_2_out = Input_A & Input_B;  // AND_Gate and_2, 32 bits wide
  Comparator #(.width(32)) comparator_2 (.a(Input_A), .b(Input_B), .lt(comparator_2_lt));  // open: gt, eq
  assign bit_extender_2_out = {{31{1'b0}}, comparator_2_lt};  // Bit_Extender bit_extender_2
  Multiplexer #(.select(3), .width(32), .enable("false")) multiplexer_1 (
    .in0(multiplexer_2_out), .in1(adder_1_out), .in2(subtractor_1_out), .in3(or_1_out), .in4(and_1_out),
    .in5(bit_extender_1_out), .out(out_6), .sel(S2S1S0));  // open: in6, in7
  Multiplexer #(.select(3), .width(32), .enable("false")) multiplexer_2 (
    .in1(adder_2_out), .in2(subtractor_2_out), .in3(or_2_out), .in4(and_2_out), .in5(bit_extender_2_out),
    .out(multiplexer_2_out), .sel(alucont_1_out_2));  // open: in0, in6, in7
  Comparator #(.width(32)) comparator_3 (.a({32{1'b0}}), .b(out_6), .eq(Zero_bit));  // open: gt, lt
endmodule

module Control (
  input  [5:0] Opcode,
  output RegWrite,
  output [1:0] RegDst,
  output ALUSrc,
  output Branch,
  output Memwrite,
  output MemToReg,
  output [2:0] ALUop,
  output Jump,
  output JAL
);

  wire and_1_out, and_2_out, not_1_out, not_2_out, not_3_out, not_4_out, not_5_out, not_6_out, not_7_out,
       not_8_out;

  not not_1 (not_1_out, Opcode[2]);
  and and_1 (and_1_out, not_1_out, not_2_out);
  not not_2 (not_2_out, Opcode[1]);
  not not_3 (not_3_out, Opcode[3]);
  and and_2 (and_2_out, not_3_out, Opcode[0]);
  not not_4 (not_4_out, Opcode[5]);
  and and_3 (RegDst[1], not_4_out, Opcode[1]);
  not not_5 (not_5_out, Opcode[3]);
  and and_4 (RegDst[0], not_5_out, not_6_out);
  not not_6 (not_6_out, Opcode[1]);
  or or_1 (ALUSrc, Opcode[1], Opcode[3]);
  and and_5 (Memwrite, Opcode[5], Opcode[3]);
  or or_2 (ALUop[0], Opcode[1], Opcode[3]);
  not not_7 (not_7_out, Opcode[5]);
  and and_6 (Jump, not_7_out, Opcode[1]);
  not not_8 (not_8_out, Opcode[5]);
  and and_7 (JAL, not_8_out, Opcode[0]);
  or or_3 (RegWrite, and_1_out, and_2_out);

  assign ALUop[2:1] = {1'b0, Opcode[2]};
  assign Branch = Opcode[2];
  assign MemToReg = Opcode[1];
endmodule

module ALUcont (
  input  [5:0] in_1,
  output [2:0] out_2
);

  wire and_1_out, and_2_out, and_3_out, not_1_out, not_2_out, not_3_out, not_4_out;

  not not_1 (not_1_out, in_1[0]);
  not not_2 (not_2_out, in_1[3]);
  not not_3 (not_3_out, in_1[2]);
  not not_4 (not_4_out, in_1[1]);
  and and_1 (and_1_out, in_1[2], not_1_out);
  and and_2 (and_2_out, not_2_out, in_1[1]);
  and and_3 (and_3_out, not_3_out, not_4_out);
  or or_1 (out_2[2], and_1_out, in_1[3]);
  or or_2 (out_2[1], in_1[0], and_2_out);
  or or_3 (out_2[0], and_3_out, in_1[0], in_1[3]);
endmodule

module General (
  input  in_1,
  input  in_2,
  input  in_3,
  input  in_4,
  input  in_5,
  input  [6:0] in_6,
  input  in_7
);

  wire clock_1_out, clock_2_out;
  wire [7:0] random_1_out, random_2_out;

  Random random_1 (.clk(clock_1_out), .out(random_1_out));  // open: next, clr
  Clock clock_1 (.out(clock_1_out));
  Random random_2 (.clk(clock_1_out), .out(random_2_out));  // open: next, clr
  RAM #(.bus("separate")) ram_1 (
    .addr(random_1_out), .din(random_2_out), .str(in_5), .clk(clock_1_out));  // open: data, sel, ld, clr
  _7_Segment_Display u_7_segment_display_1 (.g(in_4), .f(in_1), .a(in_2), .b(in_3), .dp(in_3));  // open: e, d, c
  Clock clock_2 (.out(clock_2_out));
  TTY tty_1 (.data(in_6), .clk(clock_2_out), .we(in_7));  // open: clr
  _7_Segment_Display u_7_segment_display_2 ();  // open: g, f, a, b, e, d, c, dp
endmodule

module ALU_Appendix_A (
  input  [31:0] in_1,
  input  [31:0] in_2,
  input  [2:0] in_3,
  output Zero_bit,
  output [31:0] AluRes
);

  wire [31:0] adder_1_out, and_1_out, bit_extender_1_out, multiplexer_2_out, not_1_out, or_1_out;

  Comparator #(.width(32)) comparator_1 (.a({32{1'b0}}), .b(AluRes), .eq(Zero_bit));  // open: gt, lt
  assign and_1_out = in_2 & multiplexer_2_out;  // AND_Gate and_1, 32 bits wide
  assign or_1_out = multiplexer_2_out | in_2;  // OR_Gate or_1, 32 bits wide
  Multiplexer #(.select(2), .width(32), .enable("false")) multiplexer_1 (
    .in0(and_1_out), .in1(or_1_out), .in2(adder_1_out), .in3(bit_extender_1_out), .out(AluRes),
    .sel(in_3[1:0]));
  assign not_1_out = ~in_1;  // NOT_Gate not_1, 32 bits wide
  Multiplexer #(.width(32), .enable("false")) multiplexer_2 (
    .in0(in_1), .in1(not_1_out), .out(multiplexer_2_out), .sel(in_3[2]));
  Adder #(.width(32)) adder_1 (.a(multiplexer_2_out), .b(in_2), .out(adder_1_out), .cin(in_3[2]));  // open: cout
  assign bit_extender_1_out = {{31{1'b0}}, adder_1_out[31]};  // Bit_Extender bit_extender_1

  // Notes on the sheet:
  //   A
  //   B
  //   ZERO
  //   EXTEND
  //   F 1:0
  //   F2
endmodule

// MemWrite
module sw__datapath (
  input  Reg_Write,
  input  MemWrite,
  input  [2:0] ALU_Control_010,
  input  in_4,
  input  Clear_PC,
  input  data
);

  wire alu_appendix_a_1_zero_bit, clock_1_out;
  wire [4:0] instruction_splitter_1__20_16_rt, instruction_splitter_1__25_21_rs;
  wire [15:0] instruction_splitter_1__15_0_imm;
  wire [23:0] shifter_1_out, shifter_2_out;
  wire [31:0] alu_appendix_a_1_alures, bit_extender_1_out, multiplexer_1_out, ram_1_data, reg32_1_rd1,
       reg32_1_rd2, register_1_q, rom_1_data, undriven;

  Register #(.width(32)) register_1 (.D(undriven), .Q(register_1_q), .clk(clock_1_out), .clr(Clear_PC));  // open: en
  Clock clock_1 (.out(clock_1_out));
  Shifter #(.width(24), .shift("lr")) shifter_1 (.in(register_1_q[23:0]), .\dist (5'b00010), .out(shifter_1_out));
  Adder #(.width(32)) adder_1 (.a(register_1_q), .b(32'h4));  // open: out, cin, cout
  ROM #(.addrWidth(24), .dataWidth(32)) rom_1 (.addr(shifter_1_out), .data(rom_1_data));  // open: sel
  Instruction_Splitter instruction_splitter_1 (
    .in_1(rom_1_data), ._15_0_imm(instruction_splitter_1__15_0_imm),
    ._20_16_rt(instruction_splitter_1__20_16_rt), ._25_21_rs(instruction_splitter_1__25_21_rs));  // open: _5_0_func, _15_11_rd, _25_0_jump, _31_26_OpCode
  reg32 reg32_1 (
    .A1(instruction_splitter_1__25_21_rs), .A2(instruction_splitter_1__20_16_rt),
    .A3(instruction_splitter_1__20_16_rt), .WD3(multiplexer_1_out), .RegWrite(Reg_Write),
    .Clock(clock_1_out), .RD1(reg32_1_rd1), .RD2(reg32_1_rd2));  // open: RegClear
  assign bit_extender_1_out = {{16{instruction_splitter_1__15_0_imm[15]}}, instruction_splitter_1__15_0_imm};  // Bit_Extender bit_extender_1
  Multiplexer #(.width(32), .enable("false")) multiplexer_1 (
    .in0(ram_1_data), .in1(32'h3424cd17), .out(multiplexer_1_out), .sel(data));
  ALU_Appendix_A alu_appendix_a_1 (
    .in_1(reg32_1_rd1), .in_2(bit_extender_1_out), .in_3(ALU_Control_010),
    .Zero_bit(alu_appendix_a_1_zero_bit), .AluRes(alu_appendix_a_1_alures));
  Shifter #(.width(24), .shift("lr")) shifter_2 (
    .in(alu_appendix_a_1_alures[23:0]), .\dist (5'b00010), .out(shifter_2_out));
  RAM #(.addrWidth(24), .dataWidth(32), .bus("separate")) ram_1 (
    .addr(shifter_2_out), .din(reg32_1_rd2), .data(ram_1_data), .str(MemWrite), .clk(clock_1_out), .clr(in_4));  // open: sel, ld

  // Notes on the sheet:
  //   contents of rom_1 (hex, n*v repeats v):
  //   8c020004 c0100014 2067fff7 e22025 642824 a42820 10a7000a 64202a 10800001 20050000 e2202a 853820
  //   e23822 ac670044 8c020050 8000011 20020001 ac020054
  //   This mux
  //   should be 1
  //   only to enter
  //   Zero
  //   MemWrite=1
endmodule

module or__datapath (
  input  [2:0] ALU_Control,
  input  Reg_Write,
  input  MemWrite,
  input  ALU_Src,
  input  MemToReg,
  input  [1:0] RegDst,
  input  in_7,
  input  Clear_PC,
  input  [1:0] in_9
);

  wire alu_appendix_a_1_zero_bit, clock_1_out;
  wire [4:0] instruction_splitter_1__15_11_rd, instruction_splitter_1__20_16_rt,
       instruction_splitter_1__25_21_rs, multiplexer_1_out;
  wire [15:0] instruction_splitter_1__15_0_imm;
  wire [23:0] shifter_1_out, shifter_2_out, undriven_2;
  wire [31:0] alu_appendix_a_1_alures, bit_extender_1_out, multiplexer_2_out, multiplexer_3_out,
       multiplexer_4_out, ram_1_data, reg32_1_rd1, reg32_1_rd2, register_1_q, rom_1_data, undriven;

  Register #(.width(32)) register_1 (.D(undriven), .Q(register_1_q), .clk(clock_1_out), .clr(Clear_PC));  // open: en
  Clock clock_1 (.out(clock_1_out));
  Shifter #(.width(24), .shift("lr")) shifter_1 (.in(register_1_q[23:0]), .\dist (5'b00010), .out(shifter_1_out));
  Adder #(.width(32)) adder_1 (.a(register_1_q), .b(32'h4));  // open: out, cin, cout
  ROM #(.addrWidth(24), .dataWidth(32)) rom_1 (.addr(shifter_1_out), .data(rom_1_data));  // open: sel
  Instruction_Splitter instruction_splitter_1 (
    .in_1(rom_1_data), ._15_0_imm(instruction_splitter_1__15_0_imm),
    ._15_11_rd(instruction_splitter_1__15_11_rd), ._20_16_rt(instruction_splitter_1__20_16_rt),
    ._25_21_rs(instruction_splitter_1__25_21_rs));  // open: _5_0_func, _25_0_jump, _31_26_OpCode
  reg32 reg32_1 (
    .A1(instruction_splitter_1__25_21_rs), .A2(instruction_splitter_1__20_16_rt), .A3(multiplexer_1_out),
    .WD3(multiplexer_2_out), .RegWrite(Reg_Write), .Clock(clock_1_out), .RD1(reg32_1_rd1), .RD2(reg32_1_rd2));  // open: RegClear
  Multiplexer #(.select(2), .width(5), .enable("false")) multiplexer_1 (
    .in0(instruction_splitter_1__25_21_rs), .in1(instruction_splitter_1__20_16_rt),
    .in2(instruction_splitter_1__15_11_rd), .out(multiplexer_1_out), .sel(RegDst));  // open: in3
  Multiplexer #(.select(2), .width(32), .enable("false")) multiplexer_2 (
    .in0(multiplexer_4_out), .in1(32'hffff0000), .in2(32'h12345678), .out(multiplexer_2_out), .sel(in_9));  // open: in3
  assign bit_extender_1_out = {{16{instruction_splitter_1__15_0_imm[15]}}, instruction_splitter_1__15_0_imm};  // Bit_Extender bit_extender_1
  ALU_Appendix_A alu_appendix_a_1 (
    .in_1(reg32_1_rd1), .in_2(multiplexer_3_out), .in_3(ALU_Control), .Zero_bit(alu_appendix_a_1_zero_bit),
    .AluRes(alu_appendix_a_1_alures));
  Multiplexer #(.width(32), .enable("false")) multiplexer_3 (
    .in0(reg32_1_rd2), .in1(bit_extender_1_out), .out(multiplexer_3_out), .sel(ALU_Src));
  Shifter #(.width(24), .shift("lr")) shifter_2 (.in(undriven_2), .\dist (5'b00010), .out(shifter_2_out));
  RAM #(.addrWidth(24), .dataWidth(32), .bus("separate")) ram_1 (
    .addr(shifter_2_out), .din(reg32_1_rd2), .data(ram_1_data), .str(MemWrite), .clk(clock_1_out), .clr(in_7));  // open: sel, ld
  Multiplexer #(.width(32), .enable("false")) multiplexer_4 (
    .in0(alu_appendix_a_1_alures), .in1(ram_1_data), .out(multiplexer_4_out), .sel(MemToReg));

  // Notes on the sheet:
  //   contents of rom_1 (hex, n*v repeats v):
  //   8c020004 c0100014 2067fff7 e22025 642824 a42820 10a7000a 64202a 10800001 20050000 e2202a 853820
  //   e23822 ac670044 8c020050 8000011 20020001 ac020054
  //   20:16
  //   15:11
  //   15:0
  //   01 for rt
  //   10 for rd
  //   00 for rs
  //   ALU Control of or instr is 001
  //   Zero
  //   Result
endmodule

module beq_Datapath (
  input  [2:0] ALU_Control,
  input  Branch,
  input  Reg_Write,
  input  RegDst,
  input  ALU_Src,
  input  Clear_PC,
  input  for_entering
);

  wire alu_appendix_a_1_zero_bit, and_1_out, clock_1_out;
  wire [4:0] instruction_splitter_1__15_11_rd, instruction_splitter_1__20_16_rt,
       instruction_splitter_1__25_21_rs, multiplexer_2_out;
  wire [15:0] instruction_splitter_1__15_0_imm;
  wire [23:0] shifter_1_out;
  wire [31:0] adder_1_out, adder_2_out, alu_appendix_a_1_alures, bit_extender_1_out, multiplexer_1_out,
       multiplexer_3_out, reg32_1_rd1, reg32_1_rd2, register_1_q, rom_1_data, shifter_2_out;

  Multiplexer #(.width(32), .enable("false")) multiplexer_1 (
    .in0(adder_1_out), .in1(adder_2_out), .out(multiplexer_1_out), .sel(and_1_out));
  Register #(.width(32)) register_1 (
    .D(multiplexer_1_out), .Q(register_1_q), .clk(clock_1_out), .clr(Clear_PC));  // open: en
  Clock clock_1 (.out(clock_1_out));
  Shifter #(.width(24), .shift("lr")) shifter_1 (.in(register_1_q[23:0]), .\dist (5'b00010), .out(shifter_1_out));
  Adder #(.width(32)) adder_1 (.a(register_1_q), .b(32'h4), .out(adder_1_out));  // open: cin, cout
  ROM #(.addrWidth(24), .dataWidth(32)) rom_1 (.addr(shifter_1_out), .data(rom_1_data));  // open: sel
  Instruction_Splitter instruction_splitter_1 (
    .in_1(rom_1_data), ._15_0_imm(instruction_splitter_1__15_0_imm),
    ._15_11_rd(instruction_splitter_1__15_11_rd), ._20_16_rt(instruction_splitter_1__20_16_rt),
    ._25_21_rs(instruction_splitter_1__25_21_rs));  // open: _5_0_func, _25_0_jump, _31_26_OpCode
  Multiplexer #(.width(5), .enable("false")) multiplexer_2 (
    .in0(instruction_splitter_1__25_21_rs), .in1(instruction_splitter_1__20_16_rt), .out(multiplexer_2_out),
    .sel(for_entering));
  reg32 reg32_1 (
    .A1(instruction_splitter_1__25_21_rs), .A2(instruction_splitter_1__20_16_rt), .A3(multiplexer_2_out),
    .WD3(multiplexer_3_out), .RegWrite(Reg_Write), .Clock(clock_1_out), .RD1(reg32_1_rd1), .RD2(reg32_1_rd2));  // open: RegClear
  assign bit_extender_1_out = {{16{instruction_splitter_1__15_0_imm[15]}}, instruction_splitter_1__15_0_imm};  // Bit_Extender bit_extender_1
  ALU_Appendix_A alu_appendix_a_1 (
    .in_1(reg32_1_rd1), .in_2(reg32_1_rd2), .in_3(ALU_Control), .Zero_bit(alu_appendix_a_1_zero_bit),
    .AluRes(alu_appendix_a_1_alures));
  Shifter #(.width(32)) shifter_2 (.in(bit_extender_1_out), .\dist (5'b00010), .out(shifter_2_out));
  and and_1 (and_1_out, Branch, alu_appendix_a_1_zero_bit);
  Adder #(.width(32)) adder_2 (.a(shifter_2_out), .b(adder_1_out), .out(adder_2_out));  // open: cin, cout
  Multiplexer #(.width(32), .enable("false")) multiplexer_3 (
    .in0(32'h12), .in1(32'h12), .out(multiplexer_3_out), .sel(for_entering));

  // Notes on the sheet:
  //   contents of rom_1 (hex, n*v repeats v):
  //   8c020004 c0100014 2067fff7 e22025 642824 a42820 10a7000a 64202a 10800001 20050000 e2202a 853820
  //   e23822 ac670044 8c020050 8000011 20020001 ac020054
  //   15:0
  //   for subtract
  //   ALU=010
  //   Zero
  //   data in
  //   rs=0
  //   and rt=1
  //   PC Src
endmodule

module add_Datapath (
  input  [2:0] ALU_Control,
  input  Reg_Write,
  input  MemWrite,
  input  ALU_Src,
  input  MemToReg,
  input  RegDst,
  input  in_7,
  input  Clear_PC
);

  wire alu_appendix_a_1_zero_bit, clock_1_out;
  wire [4:0] instruction_splitter_1__15_11_rd, instruction_splitter_1__20_16_rt,
       instruction_splitter_1__25_21_rs, multiplexer_1_out;
  wire [15:0] instruction_splitter_1__15_0_imm;
  wire [23:0] shifter_1_out, shifter_2_out;
  wire [31:0] adder_1_out, alu_appendix_a_1_alures, bit_extender_1_out, multiplexer_2_out, multiplexer_3_out,
       ram_1_data, reg32_1_rd1, reg32_1_rd2, register_1_q, rom_1_data;

  Register #(.width(32)) register_1 (.D(adder_1_out), .Q(register_1_q), .clk(clock_1_out), .clr(Clear_PC));  // open: en
  Clock clock_1 (.out(clock_1_out));
  Shifter #(.width(24), .shift("lr")) shifter_1 (.in(register_1_q[23:0]), .\dist (5'b00010), .out(shifter_1_out));
  Adder #(.width(32)) adder_1 (.a(register_1_q), .b(32'h4), .out(adder_1_out));  // open: cin, cout
  ROM #(.addrWidth(24), .dataWidth(32)) rom_1 (.addr(shifter_1_out), .data(rom_1_data));  // open: sel
  Instruction_Splitter instruction_splitter_1 (
    .in_1(rom_1_data), ._15_0_imm(instruction_splitter_1__15_0_imm),
    ._15_11_rd(instruction_splitter_1__15_11_rd), ._20_16_rt(instruction_splitter_1__20_16_rt),
    ._25_21_rs(instruction_splitter_1__25_21_rs));  // open: _5_0_func, _25_0_jump, _31_26_OpCode
  reg32 reg32_1 (
    .A1(instruction_splitter_1__25_21_rs), .A2(instruction_splitter_1__20_16_rt), .A3(multiplexer_1_out),
    .WD3(multiplexer_3_out), .RegWrite(Reg_Write), .Clock(clock_1_out), .RD1(reg32_1_rd1), .RD2(reg32_1_rd2));  // open: RegClear
  Multiplexer #(.width(5), .enable("false")) multiplexer_1 (
    .in0(instruction_splitter_1__20_16_rt), .in1(instruction_splitter_1__15_11_rd), .out(multiplexer_1_out),
    .sel(RegDst));
  assign bit_extender_1_out = {{16{instruction_splitter_1__15_0_imm[15]}}, instruction_splitter_1__15_0_imm};  // Bit_Extender bit_extender_1
  ALU_Appendix_A alu_appendix_a_1 (
    .in_1(reg32_1_rd1), .in_2(multiplexer_2_out), .in_3(ALU_Control), .Zero_bit(alu_appendix_a_1_zero_bit),
    .AluRes(alu_appendix_a_1_alures));
  Multiplexer #(.width(32), .enable("false")) multiplexer_2 (
    .in0(reg32_1_rd2), .in1(bit_extender_1_out), .out(multiplexer_2_out), .sel(ALU_Src));
  Shifter #(.width(24), .shift("lr")) shifter_2 (
    .in(alu_appendix_a_1_alures[23:0]), .\dist (5'b00010), .out(shifter_2_out));
  RAM #(.addrWidth(24), .dataWidth(32), .bus("separate")) ram_1 (
    .addr(shifter_2_out), .din(reg32_1_rd2), .data(ram_1_data), .str(MemWrite), .clk(clock_1_out), .clr(in_7));  // open: sel, ld
  Multiplexer #(.width(32), .enable("false")) multiplexer_3 (
    .in0(alu_appendix_a_1_alures), .in1(ram_1_data), .out(multiplexer_3_out), .sel(MemToReg));

  // Notes on the sheet:
  //   contents of rom_1 (hex, n*v repeats v):
  //   8c020004 c0100014 2067fff7 e22025 642824 a42820 10a7000a 64202a 10800001 20050000 e2202a 853820
  //   e23822 ac670044 8c020050 8000011 20020001 ac020054
  //   20:16
  //   15:11
  //   15:0
  //   Zero
  //   Result
endmodule

module addi_Datapath (
  input  [2:0] ALU_Control,
  input  Branch,
  input  Reg_Write,
  input  MemWrite,
  input  ALU_Src,
  input  MemToReg,
  input  RegDst,
  input  in_8,
  input  Clear_PC
);

  wire alu_appendix_a_1_zero_bit, and_1_out, clock_1_out;
  wire [4:0] instruction_splitter_1__15_11_rd, instruction_splitter_1__20_16_rt,
       instruction_splitter_1__25_21_rs, multiplexer_2_out;
  wire [15:0] instruction_splitter_1__15_0_imm;
  wire [23:0] shifter_1_out, shifter_3_out;
  wire [31:0] adder_1_out, adder_2_out, alu_appendix_a_1_alures, bit_extender_1_out, multiplexer_1_out,
       multiplexer_3_out, multiplexer_4_out, ram_1_data, reg32_1_rd1, reg32_1_rd2, register_1_q, rom_1_data,
       shifter_2_out;

  Multiplexer #(.width(32), .enable("false")) multiplexer_1 (
    .in0(adder_1_out), .in1(adder_2_out), .out(multiplexer_1_out), .sel(and_1_out));
  Register #(.width(32)) register_1 (
    .D(multiplexer_1_out), .Q(register_1_q), .clk(clock_1_out), .clr(Clear_PC));  // open: en
  Clock clock_1 (.out(clock_1_out));
  Shifter #(.width(24), .shift("lr")) shifter_1 (.in(register_1_q[23:0]), .\dist (5'b00010), .out(shifter_1_out));
  Adder #(.width(32)) adder_1 (.a(register_1_q), .b(32'h4), .out(adder_1_out));  // open: cin, cout
  ROM #(.addrWidth(24), .dataWidth(32)) rom_1 (.addr(shifter_1_out), .data(rom_1_data));  // open: sel
  Instruction_Splitter instruction_splitter_1 (
    .in_1(rom_1_data), ._15_0_imm(instruction_splitter_1__15_0_imm),
    ._15_11_rd(instruction_splitter_1__15_11_rd), ._20_16_rt(instruction_splitter_1__20_16_rt),
    ._25_21_rs(instruction_splitter_1__25_21_rs));  // open: _5_0_func, _25_0_jump, _31_26_OpCode
  reg32 reg32_1 (
    .A1(instruction_splitter_1__25_21_rs), .A2(instruction_splitter_1__20_16_rt), .A3(multiplexer_2_out),
    .WD3(multiplexer_4_out), .RegWrite(Reg_Write), .Clock(clock_1_out), .RD1(reg32_1_rd1), .RD2(reg32_1_rd2));  // open: RegClear
  Multiplexer #(.width(5), .enable("false")) multiplexer_2 (
    .in0(instruction_splitter_1__20_16_rt), .in1(instruction_splitter_1__15_11_rd), .out(multiplexer_2_out),
    .sel(RegDst));
  assign bit_extender_1_out = {{16{instruction_splitter_1__15_0_imm[15]}}, instruction_splitter_1__15_0_imm};  // Bit_Extender bit_extender_1
  ALU_Appendix_A alu_appendix_a_1 (
    .in_1(reg32_1_rd1), .in_2(multiplexer_3_out), .in_3(ALU_Control), .Zero_bit(alu_appendix_a_1_zero_bit),
    .AluRes(alu_appendix_a_1_alures));
  Multiplexer #(.width(32), .enable("false")) multiplexer_3 (
    .in0(reg32_1_rd2), .in1(bit_extender_1_out), .out(multiplexer_3_out), .sel(ALU_Src));
  Shifter #(.width(32)) shifter_2 (.in(bit_extender_1_out), .\dist (5'b00010), .out(shifter_2_out));
  and and_1 (and_1_out, Branch, alu_appendix_a_1_zero_bit);
  Shifter #(.width(24), .shift("lr")) shifter_3 (
    .in(alu_appendix_a_1_alures[23:0]), .\dist (5'b00010), .out(shifter_3_out));
  Adder #(.width(32)) adder_2 (.a(shifter_2_out), .b(adder_1_out), .out(adder_2_out));  // open: cin, cout
  RAM #(.addrWidth(24), .dataWidth(32), .bus("separate")) ram_1 (
    .addr(shifter_3_out), .din(reg32_1_rd2), .data(ram_1_data), .str(MemWrite), .clk(clock_1_out), .clr(in_8));  // open: sel, ld
  Multiplexer #(.width(32), .enable("false")) multiplexer_4 (
    .in0(alu_appendix_a_1_alures), .in1(ram_1_data), .out(multiplexer_4_out), .sel(MemToReg));

  // Notes on the sheet:
  //   contents of rom_1 (hex, n*v repeats v):
  //   8c020004 c0100014 2067fff7 e22025 642824 a42820 10a7000a 64202a 10800001 20050000 e2202a 853820
  //   e23822 ac670044 8c020050 8000011 20020001 ac020054
  //   20:16
  //   15:11
  //   15:0
  //   Zero
  //   Result
endmodule

module read_write (
  input  [31:0] address,
  input  [31:0] write_data,
  input  Write_En,
  output [31:0] Read_data
);

  wire Clock_out;

  Clock Clock (.out(Clock_out));
  RAM #(.addrWidth(24), .dataWidth(32), .bus("separate")) ram_1 (
    .addr(address[25:2]), .din(write_data), .data(Read_data), .str(Write_En), .sel(1'b1), .clk(Clock_out),
    .ld(1'b1), .clr(1'b0));
endmodule

module read_write_newmemory (
  input  [15:0] address,
  input  [15:0] write_data,
  input  Write_En,
  output [15:0] Read_data
);

  wire Clock_out;

  Clock Clock (.out(Clock_out));
  RAM #(.addrWidth(12), .dataWidth(16), .bus("separate")) ram_1 (
    .addr(address[12:1]), .din(write_data), .data(Read_data), .str(Write_En), .sel(1'b1), .clk(Clock_out),
    .ld(1'b1), .clr(1'b0));
endmodule
